// Digital circuit 8bit_adder.dig as structural Verilog
module _8bit_adder (
  input  A0,
  input  B0,
  input  A1,
  input  B1,
  input  A2,
  input  B2,
  input  A3,
  input  B3,
  input  A4,
  input  B4,
  input  A5,
  input  B5,
  input  A6,
  input  B6,
  input  A7,
  input  B7,
  input  C,
  output O0,
  output O1,
  output O2,
  output O3,
  output O4,
  output O5,
  output O6,
  output O7,
  output Overflow
);

  wire full_adder_1_carry, full_adder_2_carry, full_adder_3_carry, full_adder_4_carry, full_adder_5_carry,
       full_adder_6_carry, full_adder_7_carry;

  full_adder full_adder_1 (.A(B0), .B(A0), .C(C), .sum(O0), .carry(full_adder_1_carry));
  full_adder full_adder_2 (.A(B1), .B(A1), .C(full_adder_1_carry), .sum(O1), .carry(full_adder_2_carry));
  full_adder full_adder_3 (.A(B2), .B(A2), .C(full_adder_2_carry), .sum(O2), .carry(full_adder_3_carry));
  full_adder full_adder_4 (.A(B3), .B(A3), .C(full_adder_3_carry), .sum(O3), .carry(full_adder_4_carry));
  full_adder full_adder_5 (.A(B4), .B(A4), .C(full_adder_4_carry), .sum(O4), .carry(full_adder_5_carry));
  full_adder full_adder_6 (.A(B5), .B(A5), .C(full_adder_5_carry), .sum(O5), .carry(full_adder_6_carry));
  full_adder full_adder_7 (.A(B6), .B(A6), .C(full_adder_6_carry), .sum(O6), .carry(full_adder_7_carry));
  full_adder full_adder_8 (.A(B7), .B(A7), .C(full_adder_7_carry), .sum(O7), .carry(Overflow));
endmodule

/* Test case:
C A7 A6 A5 A4 A3 A2 A1 A0 B7 B6 B5 B4 B3 B2 B1 B0 Overflow O7 O6 O5 O4 O3 O2 O1 O0
repeat(65536) 0 bits(8,n>>8) bits(8,n) bits(9, (n>>8)+(n&255))
repeat(65536) 1 bits(8,n>>8) bits(8,n) bits(9, (n>>8)+(n&255)+1)
*/
