// Digital circuit 8bit_comparator.dig as structural Verilog
module _8bit_comparator (
  input  B7,
  input  A7,
  input  B6,
  input  A6,
  input  B5,
  input  A5,
  input  B4,
  input  A4,
  input  B3,
  input  A3,
  input  B2,
  input  A2,
  input  B1,
  input  A1,
  input  B0,
  input  A0,
  output A_lt_B,
  output A_gt_B,
  output A_eq_B
);

  wire and_1_out, and_2_out, and_3_out, and_4_out, and_5_out, and_6_out, and_7_out, and_8_out, and_9_out,
       and_10_out, and_11_out, and_12_out, and_13_out, and_14_out, and_15_out, and_16_out, and_17_out,
       and_18_out, and_19_out, and_20_out, and_21_out, and_22_out, and_23_out, and_24_out, and_25_out,
       and_26_out, nor_1_out, nor_2_out, nor_3_out, nor_4_out, nor_5_out, nor_6_out, nor_7_out, nor_8_out,
       not_1_out, not_2_out, not_3_out, not_4_out, not_5_out, not_6_out, not_7_out, not_8_out, not_9_out,
       not_10_out, not_11_out, not_12_out, not_13_out, not_14_out, not_15_out, not_16_out, not_17_out,
       not_18_out, or_1_out, or_2_out;

  not not_1 (not_1_out, A7);
  not not_2 (not_2_out, B7);
  not not_3 (not_3_out, A6);
  not not_4 (not_4_out, B6);
  not not_5 (not_5_out, A5);
  not not_6 (not_6_out, B5);
  not not_7 (not_7_out, A4);
  not not_8 (not_8_out, B4);
  not not_9 (not_9_out, A3);
  not not_10 (not_10_out, B3);
  not not_11 (not_11_out, A2);
  not not_12 (not_12_out, B2);
  not not_13 (not_13_out, A1);
  not not_14 (not_14_out, B1);
  not not_15 (not_15_out, A0);
  not not_16 (not_16_out, B0);
  and and_1 (and_1_out, not_1_out, B7);
  and and_2 (and_2_out, A7, not_2_out);
  and and_3 (and_3_out, not_3_out, B6);
  and and_4 (and_4_out, A6, not_4_out);
  and and_5 (and_5_out, not_5_out, B5);
  and and_6 (and_6_out, A5, not_6_out);
  and and_7 (and_7_out, not_7_out, B4);
  and and_8 (and_8_out, A4, not_8_out);
  and and_9 (and_9_out, not_9_out, B3);
  and and_10 (and_10_out, A3, not_10_out);
  and and_11 (and_11_out, not_11_out, B2);
  and and_12 (and_12_out, A2, not_12_out);
  and and_13 (and_13_out, not_13_out, B1);
  and and_14 (and_14_out, A1, not_14_out);
  and and_15 (and_15_out, not_15_out, B0);
  and and_16 (and_16_out, A0, not_16_out);
  nor nor_1 (nor_1_out, and_1_out, and_2_out);
  nor nor_2 (nor_2_out, and_3_out, and_4_out);
  nor nor_3 (nor_3_out, and_5_out, and_6_out);
  nor nor_4 (nor_4_out, and_7_out, and_8_out);
  nor nor_5 (nor_5_out, and_9_out, and_10_out);
  nor nor_6 (nor_6_out, and_11_out, and_12_out);
  nor nor_7 (nor_7_out, and_13_out, and_14_out);
  nor nor_8 (nor_8_out, and_15_out, and_16_out);
  and and_17 (and_17_out, nor_3_out, nor_4_out, nor_5_out, nor_6_out, nor_1_out);
  and and_18 (and_18_out, nor_3_out, nor_4_out, nor_5_out, nor_6_out, nor_7_out);
  and and_19 (and_19_out, nor_1_out, and_3_out);
  and and_20 (and_20_out, and_5_out, nor_1_out, nor_2_out);
  and and_21 (and_21_out, and_7_out, nor_1_out, nor_2_out, nor_3_out);
  and and_22 (and_22_out, and_9_out, nor_1_out, nor_2_out, nor_3_out, nor_4_out);
  and and_23 (and_23_out, nor_1_out, nor_2_out, nor_3_out, nor_4_out, nor_5_out);
  and and_24 (and_24_out, and_11_out, and_23_out);
  and and_25 (and_25_out, and_13_out, nor_2_out, and_17_out);
  and and_26 (and_26_out, and_15_out, nor_1_out, nor_2_out, and_18_out);
  and and_27 (A_eq_B, and_18_out, nor_1_out, nor_2_out, nor_8_out);
  or or_1 (or_1_out, and_1_out, and_19_out, and_20_out, and_21_out);
  or or_2 (or_2_out, and_22_out, and_24_out, and_25_out, and_26_out);
  or or_3 (A_lt_B, or_1_out, or_2_out);
  not not_17 (not_17_out, A_lt_B);
  not not_18 (not_18_out, A_eq_B);
  and and_28 (A_gt_B, not_17_out, not_18_out);
endmodule

/* Test case:
A7 A6 A5 A4 A3 A2 A1 A0 B7 B6 B5 B4 B3 B2 B1 B0 A<B A>B A=B
0 1 1 1 1 1 1 0 0 1 1 0 0 1 0 1 0 1 0
0 1 1 0 1 1 0 1 1 1 0 1 0 1 0 0 1 0 0
1 1 1 0 1 0 1 0 1 0 0 1 1 0 0 1 0 1 0
0 0 0 1 1 1 0 1 0 1 0 1 1 0 1 1 1 0 0
1 1 1 1 1 0 1 0 1 0 1 1 1 0 1 1 0 1 0
0 0 0 1 0 0 1 1 0 1 0 0 0 1 1 0 1 0 0
0 0 1 0 1 1 1 0 1 0 1 1 1 1 0 0 1 0 0
0 1 0 0 1 1 1 0 1 1 1 0 0 1 1 1 1 0 0
1 0 0 1 0 0 1 1 0 1 0 1 0 0 1 0 0 1 0
0 0 1 1 0 1 0 0 0 0 1 1 0 1 0 1 1 0 0
1 1 0 1 1 0 1 1 1 1 0 1 0 1 0 0 0 1 0
0 1 0 0 1 1 1 1 0 1 1 1 1 1 0 0 1 0 0
1 1 1 0 0 1 1 1 1 0 0 1 1 0 0 1 0 1 0
0 1 1 0 1 0 0 0 0 0 1 1 0 1 1 1 0 1 0
0 0 1 0 0 0 0 1 1 1 0 0 1 1 0 0 1 0 0
1 0 0 0 0 1 1 1 0 1 1 1 1 0 1 1 0 1 0
0 0 0 0 1 0 0 1 1 1 1 1 1 0 1 1 1 0 0
1 1 1 0 0 0 1 1 1 1 1 1 0 0 0 0 1 0 0
0 1 0 1 0 1 1 0 0 1 0 0 0 0 0 1 0 1 0
0 0 0 1 0 0 1 1 1 0 1 0 1 1 0 1 1 0 0
0 1 0 0 0 0 1 0 1 0 1 1 1 0 0 1 1 0 0
1 1 0 1 1 0 1 0 1 1 1 0 0 1 1 0 1 0 0
1 1 1 1 1 1 0 1 0 0 1 1 1 1 0 1 0 1 0
1 0 0 0 0 1 1 1 0 1 1 0 1 0 0 1 0 1 0
0 0 1 1 1 0 1 0 1 1 0 0 0 0 1 1 1 0 0
1 0 1 0 0 1 1 1 1 1 0 1 1 0 1 0 1 0 0
0 0 1 0 0 1 0 1 1 1 0 1 0 0 0 0 1 0 0
1 0 1 1 0 0 1 1 0 0 0 0 0 0 0 1 0 1 0
0 1 0 1 1 0 0 1 1 0 1 0 0 0 1 1 1 0 0
0 1 1 1 1 1 1 0 0 0 1 0 1 1 0 0 0 1 0
0 0 1 1 0 0 1 1 1 0 1 0 0 0 1 0 1 0 0
0 1 0 1 1 0 0 1 1 0 0 0 0 0 1 0 1 0 0
0 1 0 0 1 1 0 0 0 0 0 0 1 1 0 1 0 1 0
1 0 1 1 1 0 0 0 1 1 0 0 1 1 1 1 1 0 0
0 0 0 0 0 0 1 0 1 0 0 1 1 1 1 1 1 0 0
0 1 0 1 1 0 0 0 1 1 1 0 0 1 1 0 1 0 0
1 0 0 0 0 0 1 0 0 1 1 1 0 0 1 1 0 1 0
1 1 0 1 1 1 1 0 1 0 1 1 1 1 1 0 0 1 0
0 0 1 0 1 1 1 0 0 1 0 0 1 0 0 0 1 0 0
0 0 1 1 1 1 1 0 0 1 1 0 1 0 1 0 1 0 0
1 0 1 1 0 1 1 1 0 0 0 1 1 1 0 0 0 1 0
0 1 0 1 0 1 0 0 0 1 1 1 0 0 1 1 1 0 0
0 0 1 0 1 1 0 1 1 0 1 0 0 1 0 0 1 0 0
0 0 1 1 1 1 1 0 0 1 1 1 0 0 1 0 1 0 0
0 0 0 0 0 0 1 0 0 1 1 0 1 1 1 0 1 0 0
0 1 1 0 0 0 1 0 0 0 1 1 1 0 0 0 0 1 0
0 1 0 0 0 1 0 1 0 1 1 1 1 0 1 0 1 0 0
0 0 1 0 0 1 1 0 0 1 0 0 1 0 0 0 1 0 0
1 0 0 1 0 1 1 0 0 1 1 1 1 0 1 0 0 1 0
1 0 1 1 1 1 1 0 0 1 1 1 1 0 1 0 0 1 0
0 1 0 0 1 1 0 0 1 1 1 0 1 1 0 0 1 0 0
1 0 1 1 0 0 0 0 1 1 0 1 1 0 0 0 1 0 0
0 1 0 0 0 1 1 1 1 1 0 1 1 1 0 0 1 0 0
0 0 0 0 1 1 1 1 0 0 1 1 0 1 0 1 1 0 0
0 0 1 1 0 0 1 0 0 0 1 0 0 1 0 0 0 1 0
1 1 0 0 1 1 1 1 0 1 1 1 1 0 0 1 0 1 0
0 0 0 0 0 0 1 0 0 0 0 0 0 0 0 0 0 1 0
0 1 1 0 1 0 0 1 0 0 0 1 0 1 0 1 0 1 0
0 1 0 1 0 1 0 1 0 0 1 1 0 1 1 1 0 1 0
0 0 0 0 0 0 0 0 1 0 1 0 1 0 1 1 1 0 0
1 0 1 1 0 0 1 0 0 1 0 1 0 0 1 0 0 1 0
0 0 1 0 1 0 1 1 1 0 1 1 0 0 1 0 1 0 0
1 1 1 1 1 1 1 1 1 0 1 1 0 1 0 0 0 1 0
1 1 1 1 0 1 0 0 0 0 1 0 1 1 0 0 0 1 0
0 0 0 0 1 1 1 1 1 1 0 1 0 0 1 0 1 0 0
1 1 1 0 0 0 0 0 0 0 1 1 0 1 1 0 0 1 0
1 1 1 0 1 0 1 0 0 1 1 0 0 1 0 1 0 1 0
1 1 1 1 0 1 0 0 1 0 1 0 1 0 1 0 0 1 0
0 0 1 0 0 0 1 1 1 1 0 1 1 0 1 0 1 0 0
0 1 1 1 1 1 1 0 1 1 1 0 0 0 0 0 1 0 0
0 1 0 0 1 1 1 1 0 1 0 1 0 1 0 0 1 0 0
0 1 1 0 1 1 0 0 0 1 1 1 0 1 1 0 1 0 0
1 0 0 1 0 1 1 1 0 1 0 0 1 0 0 1 0 1 0
0 0 1 1 1 1 0 1 0 0 1 1 1 1 1 1 1 0 0
1 0 1 0 1 1 1 0 1 0 0 1 0 1 1 1 0 1 0
1 0 0 1 1 0 0 1 0 1 1 1 0 1 1 1 0 1 0
1 1 1 0 0 1 1 1 0 0 0 1 0 1 0 0 0 1 0
1 0 1 0 0 1 0 0 1 0 0 1 0 0 1 1 0 1 0
0 1 0 1 0 0 0 1 1 1 0 0 0 0 0 1 1 0 0
1 1 0 1 0 1 1 0 0 1 0 1 0 1 0 0 0 1 0
0 1 0 1 1 0 0 0 0 1 1 1 1 1 1 0 1 0 0
1 1 1 0 0 1 0 1 0 0 0 0 0 1 0 1 0 1 0
1 1 1 0 1 1 0 0 1 0 1 1 0 1 0 0 0 1 0
0 0 0 0 1 0 0 1 0 1 1 1 0 1 1 0 1 0 0
0 0 1 1 1 1 1 0 0 0 0 0 1 1 0 0 0 1 0
0 1 0 0 0 1 1 0 0 1 1 1 0 0 1 0 1 0 0
0 1 1 1 1 1 0 1 1 0 1 0 1 0 1 0 1 0 0
0 1 0 0 1 1 1 0 0 1 1 0 0 0 1 1 1 0 0
0 0 1 0 1 1 0 0 1 0 1 1 0 1 1 0 1 0 0
0 1 0 0 1 1 1 1 0 0 1 0 0 1 1 0 0 1 0
1 1 0 1 1 0 0 1 0 0 0 1 1 1 0 1 0 1 0
0 0 0 1 0 1 1 1 0 1 0 1 1 1 0 0 1 0 0
0 1 0 1 1 1 0 0 0 0 0 0 0 0 0 0 0 1 0
0 1 1 1 0 0 1 0 0 0 1 0 0 0 1 1 0 1 0
0 0 0 0 0 0 0 1 1 0 0 1 1 1 0 1 1 0 0
0 0 1 0 0 0 0 1 0 0 1 1 1 1 0 1 1 0 0
1 1 1 0 0 0 0 1 0 1 1 1 0 0 1 1 0 1 0
1 1 1 0 1 1 1 0 0 1 1 1 0 0 0 0 0 1 0
0 0 0 0 1 1 1 0 0 1 0 1 0 0 0 1 1 0 0
0 1 1 1 0 1 1 0 0 0 0 1 0 1 0 1 0 1 0
0 0 1 0 1 1 0 1 1 1 1 0 1 0 0 1 1 0 0
1 0 0 1 0 0 0 1 0 0 1 1 0 0 0 0 0 1 0
0 1 1 0 1 1 0 1 1 0 0 0 0 0 1 1 1 0 0
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*/
