// Digital circuit alu.dig as structural Verilog
module alu (
  input  A0,
  input  A1,
  input  A2,
  input  A3,
  input  A4,
  input  A5,
  input  A6,
  input  A7,
  input  B0,
  input  B1,
  input  B2,
  input  B3,
  input  B4,
  input  B5,
  input  B6,
  input  B7,
  input  OPT0,
  input  OPT1,
  input  OPT2,
  input  OPT3,
  output O0,
  output O1,
  output O2,
  output O3,
  output O4,
  output O5,
  output O6,
  output O7,
  output P0,
  output P1,
  output P2,
  output P3,
  output P4,
  output P5,
  output P6,
  output P7,
  output F_OF,
  output F_Z,
  output F_LZ,
  output F_GZ,
  output F_PAR,
  output F_DIV0
);

  wire and_1_out, and_2_out, and_3_out, and_4_out, and_5_out, and_6_out, and_7_out, and_8_out, and_9_out,
       and_10_out, and_11_out, and_12_out, and_13_out, and_14_out, and_15_out, and_16_out, and_17_out,
       and_18_out, and_19_out, and_20_out, and_21_out, and_22_out, and_23_out, and_24_out, and_25_out,
       and_26_out, and_27_out, and_28_out, and_29_out, and_30_out, and_31_out, and_32_out, and_33_out,
       and_34_out, and_35_out, and_36_out, and_37_out, and_38_out, and_39_out, and_40_out, and_41_out,
       and_42_out, and_43_out, and_44_out, and_45_out, and_46_out, and_47_out, and_48_out, and_49_out,
       and_50_out, and_51_out, and_52_out, and_53_out, and_54_out, and_55_out, and_56_out, and_57_out,
       and_58_out, and_59_out, and_60_out, and_61_out, and_62_out, and_63_out, and_64_out, and_65_out,
       and_66_out, and_67_out, and_68_out, and_69_out, and_70_out, and_71_out, and_72_out, and_73_out,
       and_74_out, and_75_out, and_76_out, and_77_out, and_78_out, and_79_out, and_80_out, and_81_out,
       and_82_out, and_83_out, and_84_out, and_85_out, and_86_out, and_87_out, and_88_out, and_89_out,
       and_90_out, and_91_out, and_92_out, and_93_out, and_94_out, and_95_out, and_96_out, and_97_out,
       and_98_out, and_99_out, and_100_out, and_101_out, and_102_out, and_103_out, and_104_out, and_105_out,
       and_106_out, and_107_out, and_108_out, and_109_out, and_110_out, and_111_out, and_112_out,
       and_113_out, and_114_out, and_115_out, and_116_out, and_117_out, and_118_out, and_119_out,
       and_120_out, and_122_out, and_123_out, and_124_out, and_125_out, and_126_out, and_127_out,
       and_128_out, and_129_out, and_130_out, and_131_out, and_132_out, and_133_out, and_134_out,
       and_135_out, and_136_out, and_137_out, and_138_out, barell_shift_right_1_o0, barell_shift_right_1_o1,
       barell_shift_right_1_o2, barell_shift_right_1_o3, barell_shift_right_1_o4, barell_shift_right_1_o5,
       barell_shift_right_1_o6, barell_shift_right_1_o7, barrel_shift_left_1_o0, barrel_shift_left_1_o1,
       barrel_shift_left_1_o2, barrel_shift_left_1_o3, barrel_shift_left_1_o4, barrel_shift_left_1_o5,
       barrel_shift_left_1_o6, barrel_shift_left_1_o7, dividor_1_div0, dividor_1_m0, dividor_1_m1,
       dividor_1_m2, dividor_1_m3, dividor_1_m4, dividor_1_m5, dividor_1_m6, dividor_1_o0, dividor_1_o1,
       dividor_1_o2, dividor_1_o3, dividor_1_o4, dividor_1_o5, dividor_1_o6, dividor_1_sgn, multiplier_1_o0,
       multiplier_1_o1, multiplier_1_o2, multiplier_1_o3, multiplier_1_o4, multiplier_1_o5, multiplier_1_o6,
       multiplier_1_o7, multiplier_1_o8, multiplier_1_o9, multiplier_1_o10, multiplier_1_o11,
       multiplier_1_o12, multiplier_1_o13, multiplier_1_sgn, not_1_out, not_2_out, not_3_out, not_4_out,
       not_5_out, not_6_out, not_7_out, not_8_out, not_9_out, not_10_out, or_1_out, or_2_out, or_3_out,
       or_4_out, or_5_out, or_6_out, or_7_out, or_8_out, or_9_out, or_10_out, or_11_out, or_12_out,
       or_13_out, or_14_out, or_15_out, or_16_out, or_17_out, or_18_out, or_19_out, or_20_out, or_21_out,
       or_22_out, or_23_out, or_24_out, or_25_out, or_26_out, or_27_out, or_28_out, or_29_out, or_30_out,
       or_31_out, or_32_out, or_33_out, or_34_out, or_35_out, or_53_out, or_54_out, or_55_out, or_57_out,
       signed_8bit_adder_1_o0, signed_8bit_adder_1_o1, signed_8bit_adder_1_o2, signed_8bit_adder_1_o3,
       signed_8bit_adder_1_o4, signed_8bit_adder_1_o5, signed_8bit_adder_1_o6, signed_8bit_adder_1_o7,
       signed_8bit_adder_1_sgn, signed_8bit_adder_2_o0, signed_8bit_adder_2_o1, signed_8bit_adder_2_o2,
       signed_8bit_adder_2_o3, signed_8bit_adder_2_o4, signed_8bit_adder_2_o5, signed_8bit_adder_2_o6,
       signed_8bit_adder_2_o7, signed_8bit_adder_2_sgn, two_complement_1_o0, two_complement_1_o1,
       two_complement_1_o2, two_complement_1_o3, two_complement_1_o4, two_complement_1_o5,
       two_complement_1_o6, two_complement_1_sgn, xor_1_out, xor_2_out, xor_3_out, xor_4_out, xor_5_out,
       xor_6_out, xor_7_out, xor_8_out;

  and and_1 (and_1_out, ~OPT3, ~OPT2, ~OPT1, ~OPT0);  // And
  and and_2 (and_2_out, ~OPT3, ~OPT2, ~OPT1, OPT0);  // And
  and and_3 (and_3_out, ~OPT3, ~OPT2, OPT1, ~OPT0);  // And
  and and_4 (and_4_out, ~OPT3, ~OPT2, OPT1, OPT0);  // And
  and and_5 (and_5_out, ~OPT3, OPT2, ~OPT1);  // And
  and and_6 (and_6_out, ~OPT3, OPT2, OPT1);  // And
  and and_7 (and_7_out, OPT3, ~OPT2, ~OPT1, ~OPT0);  // And
  and and_8 (and_8_out, OPT3, ~OPT2, ~OPT1, OPT0);  // And
  and and_9 (and_9_out, OPT3, ~OPT2, OPT1, ~OPT0);  // And
  and and_10 (and_10_out, OPT3, ~OPT2, OPT1, OPT0);  // And
  and and_11 (and_11_out, OPT3, OPT2, ~OPT1, ~OPT0);  // And
  and and_12 (and_12_out, OPT3, OPT2, ~OPT1, OPT0);  // And
  and and_13 (and_13_out, OPT3, OPT2, OPT1, ~OPT0);  // And
  and and_14 (and_14_out, OPT3, OPT2, OPT1, OPT0);
  or or_1 (or_1_out, and_15_out, and_24_out);
  and and_15 (and_15_out, and_1_out, B7);
  signed_8bit_adder signed_8bit_adder_1 (
    .A0(A0), .B0(1'b1), .A1(A1), .B1(1'b0), .A2(A2), .B2(1'b0), .A3(A3), .B3(1'b0), .A4(A4), .B4(1'b0),
    .A5(A5), .B5(1'b0), .A6(A6), .B6(1'b0), .A7(A7), .B7(and_14_out), .o0(signed_8bit_adder_1_o0),
    .o1(signed_8bit_adder_1_o1), .o2(signed_8bit_adder_1_o2), .o3(signed_8bit_adder_1_o3),
    .o4(signed_8bit_adder_1_o4), .o5(signed_8bit_adder_1_o5), .o6(signed_8bit_adder_1_o6),
    .o7(signed_8bit_adder_1_o7), .sgn(signed_8bit_adder_1_sgn));
  two_complement two_complement_1 (
    .A8(A7), .A6(A6), .A5(A5), .A4(A4), .A3(A3), .A2(A2), .A1(A1), .A0(A0), .A7(1'b0),
    .O0(two_complement_1_o0), .O1(two_complement_1_o1), .O2(two_complement_1_o2), .O3(two_complement_1_o3),
    .O4(two_complement_1_o4), .O5(two_complement_1_o5), .O6(two_complement_1_o6), .sgn(two_complement_1_sgn));  // open: O7
  not not_1 (not_1_out, A7);
  not not_2 (not_2_out, A6);
  not not_3 (not_3_out, A5);
  not not_4 (not_4_out, A4);
  not not_5 (not_5_out, A3);
  not not_6 (not_6_out, A2);
  not not_7 (not_7_out, A1);
  not not_8 (not_8_out, A0);
  xor xor_1 (xor_1_out, A7, B7);
  xor xor_2 (xor_2_out, A6, B6);
  xor xor_3 (xor_3_out, A5, B5);
  xor xor_4 (xor_4_out, A4, B4);
  xor xor_5 (xor_5_out, A3, B3);
  xor xor_6 (xor_6_out, A2, B2);
  xor xor_7 (xor_7_out, A1, B1);
  xor xor_8 (xor_8_out, A0, B0);
  or or_2 (or_2_out, A7, B7);
  or or_3 (or_3_out, A6, B6);
  or or_4 (or_4_out, A5, B5);
  or or_5 (or_5_out, A4, B4);
  or or_6 (or_6_out, A3, B3);
  or or_7 (or_7_out, A2, B2);
  or or_8 (or_8_out, A1, B1);
  or or_9 (or_9_out, A0, B0);
  and and_16 (and_16_out, A7, B7);
  and and_17 (and_17_out, A6, B6);
  and and_18 (and_18_out, A5, B5);
  and and_19 (and_19_out, A4, B4);
  and and_20 (and_20_out, A3, B3);
  and and_21 (and_21_out, A2, B2);
  and and_22 (and_22_out, A1, B1);
  and and_23 (and_23_out, A0, B0);
  barell_shift_right barell_shift_right_1 (
    .A0(A0), .A1(A1), .A2(A2), .A3(A3), .A4(A4), .A5(A5), .A6(A6), .A7(A7), .B0(B0), .B1(B1), .B2(B2),
    .ROT(OPT0), .O0(barell_shift_right_1_o0), .O1(barell_shift_right_1_o1), .O2(barell_shift_right_1_o2),
    .O3(barell_shift_right_1_o3), .O4(barell_shift_right_1_o4), .O5(barell_shift_right_1_o5),
    .O6(barell_shift_right_1_o6), .O7(barell_shift_right_1_o7));
  barrel_shift_left barrel_shift_left_1 (
    .A0(A0), .A1(A1), .A2(A2), .A3(A3), .A4(A4), .A5(A5), .A6(A6), .A7(A7), .B0(B0), .B1(B1), .B2(B2),
    .ROT(OPT0), .O0(barrel_shift_left_1_o0), .O1(barrel_shift_left_1_o1), .O2(barrel_shift_left_1_o2),
    .O3(barrel_shift_left_1_o3), .O4(barrel_shift_left_1_o4), .O5(barrel_shift_left_1_o5),
    .O6(barrel_shift_left_1_o6), .O7(barrel_shift_left_1_o7));
  dividor dividor_1 (
    .A0(A0), .B0(B0), .A1(A1), .B1(B1), .A2(A2), .B2(B2), .A3(A3), .B3(B3), .A4(A4), .B4(B4), .A5(A5),
    .B5(B5), .A6(A6), .B6(B6), .A7(A7), .B7(B7), .o6(dividor_1_o6), .o5(dividor_1_o5), .o4(dividor_1_o4),
    .o3(dividor_1_o3), .o2(dividor_1_o2), .o1(dividor_1_o1), .o0(dividor_1_o0), .m0(dividor_1_m0),
    .m1(dividor_1_m1), .m2(dividor_1_m2), .m3(dividor_1_m3), .m4(dividor_1_m4), .m5(dividor_1_m5),
    .m6(dividor_1_m6), .sgn(dividor_1_sgn), .div0(dividor_1_div0));
  multiplier multiplier_1 (
    .a0(A0), .a1(A1), .a2(A2), .a3(A3), .a4(A4), .a5(A5), .a6(A6), .b0(B0), .b1(B1), .b2(B2), .b3(B3),
    .b4(B4), .b5(B5), .b6(B6), .a7(A7), .b7(B7), .o0(multiplier_1_o0), .o1(multiplier_1_o1),
    .o2(multiplier_1_o2), .o3(multiplier_1_o3), .o4(multiplier_1_o4), .o5(multiplier_1_o5),
    .o6(multiplier_1_o6), .o7(multiplier_1_o7), .o8(multiplier_1_o8), .o9(multiplier_1_o9),
    .o10(multiplier_1_o10), .o11(multiplier_1_o11), .o12(multiplier_1_o12), .o13(multiplier_1_o13),
    .sgn(multiplier_1_sgn));
  signed_8bit_adder signed_8bit_adder_2 (
    .A0(A0), .B0(B0), .A1(A1), .B1(B1), .A2(A2), .B2(B2), .A3(A3), .B3(B3), .A4(A4), .B4(B4), .A5(A5),
    .B5(B5), .A6(A6), .B6(B6), .A7(A7), .B7(or_1_out), .o0(signed_8bit_adder_2_o0),
    .o1(signed_8bit_adder_2_o1), .o2(signed_8bit_adder_2_o2), .o3(signed_8bit_adder_2_o3),
    .o4(signed_8bit_adder_2_o4), .o5(signed_8bit_adder_2_o5), .o6(signed_8bit_adder_2_o6),
    .o7(signed_8bit_adder_2_o7), .sgn(signed_8bit_adder_2_sgn));
  and and_24 (and_24_out, and_2_out, not_9_out);
  not not_9 (not_9_out, B7);
  or or_10 (or_10_out, and_1_out, and_2_out);
  or or_11 (or_11_out, and_14_out, and_13_out);
  and and_25 (and_25_out, signed_8bit_adder_2_o0, or_10_out);
  and and_26 (and_26_out, signed_8bit_adder_2_o1, or_10_out);
  and and_27 (and_27_out, signed_8bit_adder_2_o2, or_10_out);
  and and_28 (and_28_out, signed_8bit_adder_2_o3, or_10_out);
  and and_29 (and_29_out, signed_8bit_adder_2_o4, or_10_out);
  and and_30 (and_30_out, signed_8bit_adder_2_o5, or_10_out);
  and and_31 (and_31_out, signed_8bit_adder_2_o6, or_10_out);
  and and_32 (and_32_out, signed_8bit_adder_2_o7, or_10_out);
  and and_33 (and_33_out, signed_8bit_adder_2_sgn, or_10_out);
  and and_34 (and_34_out, signed_8bit_adder_1_sgn, or_11_out);
  and and_35 (and_35_out, signed_8bit_adder_1_o6, or_11_out);
  and and_36 (and_36_out, signed_8bit_adder_1_o5, or_11_out);
  and and_37 (and_37_out, signed_8bit_adder_1_o4, or_11_out);
  and and_38 (and_38_out, signed_8bit_adder_1_o3, or_11_out);
  and and_39 (and_39_out, signed_8bit_adder_1_o2, or_11_out);
  and and_40 (and_40_out, signed_8bit_adder_1_o1, or_11_out);
  and and_41 (and_41_out, signed_8bit_adder_1_o0, or_11_out);
  and and_42 (and_42_out, two_complement_1_sgn, and_12_out);
  and and_43 (and_43_out, two_complement_1_o6, and_12_out);
  and and_44 (and_44_out, two_complement_1_o5, and_12_out);
  and and_45 (and_45_out, two_complement_1_o4, and_12_out);
  and and_46 (and_46_out, two_complement_1_o3, and_12_out);
  and and_47 (and_47_out, two_complement_1_o2, and_12_out);
  and and_48 (and_48_out, two_complement_1_o1, and_12_out);
  and and_49 (and_49_out, two_complement_1_o0, and_12_out);
  and and_50 (and_50_out, A7, and_11_out);
  and and_51 (and_51_out, A6, and_11_out);
  and and_52 (and_52_out, A5, and_11_out);
  and and_53 (and_53_out, A4, and_11_out);
  and and_54 (and_54_out, A3, and_11_out);
  and and_55 (and_55_out, A2, and_11_out);
  and and_56 (and_56_out, A1, and_11_out);
  and and_57 (and_57_out, A0, and_11_out);
  and and_58 (and_58_out, not_1_out, and_10_out);
  and and_59 (and_59_out, not_2_out, and_10_out);
  and and_60 (and_60_out, not_3_out, and_10_out);
  and and_61 (and_61_out, not_4_out, and_10_out);
  and and_62 (and_62_out, not_5_out, and_10_out);
  and and_63 (and_63_out, not_6_out, and_10_out);
  and and_64 (and_64_out, not_7_out, and_10_out);
  and and_65 (and_65_out, not_8_out, and_10_out);
  and and_66 (and_66_out, xor_1_out, and_9_out);
  and and_67 (and_67_out, xor_2_out, and_9_out);
  and and_68 (and_68_out, xor_3_out, and_9_out);
  and and_69 (and_69_out, xor_4_out, and_9_out);
  and and_70 (and_70_out, xor_5_out, and_9_out);
  and and_71 (and_71_out, xor_6_out, and_9_out);
  and and_72 (and_72_out, xor_7_out, and_9_out);
  and and_73 (and_73_out, xor_8_out, and_9_out);
  and and_74 (and_74_out, or_2_out, and_8_out);
  and and_75 (and_75_out, or_3_out, and_8_out);
  and and_76 (and_76_out, or_4_out, and_8_out);
  and and_77 (and_77_out, or_5_out, and_8_out);
  and and_78 (and_78_out, or_6_out, and_8_out);
  and and_79 (and_79_out, or_7_out, and_8_out);
  and and_80 (and_80_out, or_8_out, and_8_out);
  and and_81 (and_81_out, or_9_out, and_8_out);
  and and_82 (and_82_out, and_16_out, and_7_out);
  and and_83 (and_83_out, and_17_out, and_7_out);
  and and_84 (and_84_out, and_18_out, and_7_out);
  and and_85 (and_85_out, and_19_out, and_7_out);
  and and_86 (and_86_out, and_20_out, and_7_out);
  and and_87 (and_87_out, and_21_out, and_7_out);
  and and_88 (and_88_out, and_22_out, and_7_out);
  and and_89 (and_89_out, and_23_out, and_7_out);
  and and_90 (and_90_out, barell_shift_right_1_o0, and_6_out);
  and and_91 (and_91_out, barell_shift_right_1_o1, and_6_out);
  and and_92 (and_92_out, barell_shift_right_1_o2, and_6_out);
  and and_93 (and_93_out, barell_shift_right_1_o3, and_6_out);
  and and_94 (and_94_out, barell_shift_right_1_o4, and_6_out);
  and and_95 (and_95_out, barell_shift_right_1_o5, and_6_out);
  and and_96 (and_96_out, barell_shift_right_1_o6, and_6_out);
  and and_97 (and_97_out, barell_shift_right_1_o7, and_6_out);
  and and_98 (and_98_out, barrel_shift_left_1_o0, and_5_out);
  and and_99 (and_99_out, barrel_shift_left_1_o1, and_5_out);
  and and_100 (and_100_out, barrel_shift_left_1_o2, and_5_out);
  and and_101 (and_101_out, barrel_shift_left_1_o3, and_5_out);
  and and_102 (and_102_out, barrel_shift_left_1_o4, and_5_out);
  and and_103 (and_103_out, barrel_shift_left_1_o5, and_5_out);
  and and_104 (and_104_out, barrel_shift_left_1_o6, and_5_out);
  and and_105 (and_105_out, barrel_shift_left_1_o7, and_5_out);
  and and_106 (and_106_out, dividor_1_o6, and_4_out);
  and and_107 (and_107_out, dividor_1_o5, and_4_out);
  and and_108 (and_108_out, dividor_1_o4, and_4_out);
  and and_109 (and_109_out, dividor_1_o3, and_4_out);
  and and_110 (and_110_out, dividor_1_o2, and_4_out);
  and and_111 (and_111_out, dividor_1_o1, and_4_out);
  and and_112 (and_112_out, dividor_1_o0, and_4_out);
  and and_113 (and_113_out, dividor_1_m0, and_4_out);
  and and_114 (and_114_out, dividor_1_m1, and_4_out);
  and and_115 (and_115_out, dividor_1_m2, and_4_out);
  and and_116 (and_116_out, dividor_1_m3, and_4_out);
  and and_117 (and_117_out, dividor_1_m4, and_4_out);
  and and_118 (and_118_out, dividor_1_m5, and_4_out);
  and and_119 (and_119_out, dividor_1_m6, and_4_out);
  and and_120 (and_120_out, dividor_1_sgn, and_4_out);
  and and_121 (F_DIV0, dividor_1_div0, and_4_out);
  and and_122 (and_122_out, multiplier_1_o0, and_3_out);
  and and_123 (and_123_out, multiplier_1_o1, and_3_out);
  and and_124 (and_124_out, multiplier_1_o2, and_3_out);
  and and_125 (and_125_out, multiplier_1_o3, and_3_out);
  and and_126 (and_126_out, multiplier_1_o4, and_3_out);
  and and_127 (and_127_out, multiplier_1_o5, and_3_out);
  and and_128 (and_128_out, multiplier_1_o6, and_3_out);
  and and_129 (and_129_out, multiplier_1_o7, and_3_out);
  and and_130 (and_130_out, multiplier_1_o8, and_3_out);
  and and_131 (and_131_out, multiplier_1_o9, and_3_out);
  and and_132 (and_132_out, multiplier_1_o10, and_3_out);
  and and_133 (and_133_out, multiplier_1_o11, and_3_out);
  and and_134 (and_134_out, multiplier_1_o12, and_3_out);
  and and_135 (and_135_out, multiplier_1_o13, and_3_out);
  and and_136 (and_136_out, multiplier_1_sgn, and_3_out);
  or or_12 (or_12_out, and_34_out, and_50_out, and_42_out);
  or or_13 (or_13_out, and_35_out, and_51_out, and_43_out);
  or or_14 (or_14_out, and_36_out, and_52_out, and_44_out);
  or or_15 (or_15_out, and_37_out, and_53_out, and_45_out);
  or or_16 (or_16_out, and_38_out, and_54_out, and_46_out);
  or or_17 (or_17_out, and_39_out, and_47_out, and_55_out);
  or or_18 (or_18_out, and_40_out, and_48_out, and_56_out);
  or or_19 (or_19_out, and_41_out, and_49_out, and_57_out);
  or or_20 (or_20_out, and_58_out, and_66_out, and_74_out, and_82_out);
  or or_21 (or_21_out, and_59_out, and_67_out, and_75_out, and_83_out);
  or or_22 (or_22_out, and_60_out, and_68_out, and_76_out, and_84_out);
  or or_23 (or_23_out, and_61_out, and_69_out, and_77_out, and_85_out);
  or or_24 (or_24_out, and_62_out, and_70_out, and_78_out, and_86_out);
  or or_25 (or_25_out, and_63_out, and_71_out, and_79_out, and_87_out);
  or or_26 (or_26_out, and_64_out, and_72_out, and_80_out, and_88_out);
  or or_27 (or_27_out, and_65_out, and_73_out, and_81_out, and_89_out);
  or or_28 (or_28_out, and_90_out, and_98_out, or_19_out);
  or or_29 (or_29_out, and_91_out, and_99_out, or_18_out);
  or or_30 (or_30_out, and_92_out, and_100_out, or_17_out);
  or or_31 (or_31_out, and_93_out, and_101_out, or_16_out);
  or or_32 (or_32_out, and_94_out, and_102_out, or_15_out);
  or or_33 (or_33_out, and_95_out, and_103_out, or_14_out);
  or or_34 (or_34_out, and_96_out, and_104_out, or_13_out);
  or or_35 (or_35_out, and_97_out, and_105_out, or_12_out);
  or or_36 (P7, 1'b0, 1'b0, 1'b0, and_120_out, and_136_out);
  or or_37 (P6, 1'b0, 1'b0, 1'b0, and_119_out, 1'b0);
  or or_38 (P5, 1'b0, 1'b0, 1'b0, and_118_out, and_135_out);
  or or_39 (P4, 1'b0, 1'b0, 1'b0, and_117_out, and_134_out);
  or or_40 (P3, 1'b0, 1'b0, 1'b0, and_116_out, and_133_out);
  or or_41 (P2, 1'b0, 1'b0, 1'b0, and_115_out, and_132_out);
  or or_42 (P1, 1'b0, 1'b0, 1'b0, and_114_out, and_131_out);
  or or_43 (P0, 1'b0, 1'b0, 1'b0, and_113_out, and_130_out);
  or or_44 (O7, or_20_out, or_35_out, and_120_out, and_129_out, and_33_out);
  or or_45 (O6, or_21_out, or_34_out, and_106_out, and_128_out, and_31_out);
  or or_46 (O5, or_22_out, or_33_out, and_107_out, and_127_out, and_30_out);
  or or_47 (O4, or_23_out, or_32_out, and_108_out, and_126_out, and_29_out);
  or or_48 (O3, or_24_out, or_31_out, and_109_out, and_125_out, and_28_out);
  or or_49 (O2, or_25_out, or_30_out, and_110_out, and_124_out, and_27_out);
  or or_50 (O1, or_26_out, or_29_out, and_111_out, and_123_out, and_26_out);
  or or_51 (F_PAR, or_27_out, or_28_out, and_112_out, and_122_out, and_25_out);
  or or_52 (F_OF, signed_8bit_adder_1_o7, and_32_out);
  not not_10 (not_10_out, and_3_out);
  or or_53 (or_53_out, P4, P5, P6);
  or or_54 (or_54_out, P0, P1, P2, P3);
  and and_137 (and_137_out, P7, and_3_out);
  and and_138 (and_138_out, O7, not_10_out);
  nor nor_1 (F_Z, or_57_out, or_55_out, or_54_out, or_53_out);
  or or_55 (or_55_out, O4, O5, O6, O7);
  or or_56 (F_LZ, and_137_out, and_138_out);
  or or_57 (or_57_out, F_PAR, O1, O2, O3);
  nor nor_2 (F_GZ, F_Z, F_LZ);

  assign O0 = F_PAR;

  // Notes on the sheet:
  //   OPT CODES:
  //   0000 ADD
  //   0001 SUB
  //   0010 MUL
  //   0011 DIVMOD
  //   0100 SHL
  //   0101 ROTL
  //   0110 SHR
  //   0111 ROTR
  //   1000 AND
  //   1001 OR
  //   1010 XOR
  //   1011 NOT
  //   1100 PASS
  //   1101 COMPL
  //   1110 INC
  //   1111 DEC
  //   Add
  //   Sub
  //   Mul
  //   DivMod
  //   ShiftLeft
  //   ShiftRight
  //   And
  //   Or
  //   Xor
  //   Not
  //   Pass
  //   Compl
  //   Inc
  //   Dec
endmodule
