// Digital circuit barell_shift_right.dig as structural Verilog
module barell_shift_right (
  input  A0,
  input  A1,
  input  A2,
  input  A3,
  input  A4,
  input  A5,
  input  A6,
  input  A7,
  input  B0,
  input  B1,
  input  B2,
  input  ROT,
  output O0,
  output O1,
  output O2,
  output O3,
  output O4,
  output O5,
  output O6,
  output O7
);

  wire and_1_out, and_2_out, and_3_out, and_4_out, and_5_out, and_6_out, and_7_out, and_8_out, and_9_out,
       and_10_out, and_11_out, and_12_out, and_13_out, and_14_out, and_15_out, and_16_out, and_17_out,
       and_18_out, and_19_out, and_20_out, and_21_out, and_22_out, and_23_out, and_24_out, and_25_out,
       and_26_out, and_27_out, and_28_out, and_29_out, and_30_out, and_31_out, and_32_out, and_33_out,
       and_34_out, and_35_out, and_36_out, and_37_out, and_38_out, and_39_out, and_40_out, and_41_out,
       and_42_out, and_43_out, and_44_out, and_45_out, and_46_out, and_47_out, and_48_out, and_49_out,
       and_50_out, and_51_out, and_52_out, and_53_out, and_54_out, and_55_out, not_1_out, not_2_out,
       not_3_out, not_4_out, not_5_out, not_6_out, or_1_out, or_2_out, or_3_out, or_4_out, or_5_out,
       or_6_out, or_7_out, or_8_out, or_9_out, or_10_out, or_11_out, or_12_out, or_13_out, or_14_out,
       or_15_out, or_16_out;

  not not_1 (not_1_out, B0);
  and and_1 (and_1_out, A0, ROT);
  not not_2 (not_2_out, not_1_out);
  and and_2 (and_2_out, not_1_out, A7);
  and and_3 (and_3_out, not_1_out, A6);
  and and_4 (and_4_out, not_1_out, A5);
  and and_5 (and_5_out, not_1_out, A4);
  and and_6 (and_6_out, not_1_out, A3);
  and and_7 (and_7_out, not_1_out, A2);
  and and_8 (and_8_out, not_1_out, A1);
  and and_9 (and_9_out, not_1_out, A0);
  and and_10 (and_10_out, not_2_out, and_1_out);
  and and_11 (and_11_out, not_2_out, A7);
  and and_12 (and_12_out, not_2_out, A6);
  and and_13 (and_13_out, not_2_out, A5);
  and and_14 (and_14_out, not_2_out, A4);
  and and_15 (and_15_out, not_2_out, A3);
  and and_16 (and_16_out, not_2_out, A2);
  and and_17 (and_17_out, not_2_out, A1);
  or or_1 (or_1_out, and_2_out, and_10_out);
  or or_2 (or_2_out, and_3_out, and_11_out);
  or or_3 (or_3_out, and_4_out, and_12_out);
  or or_4 (or_4_out, and_5_out, and_13_out);
  or or_5 (or_5_out, and_6_out, and_14_out);
  or or_6 (or_6_out, and_7_out, and_15_out);
  or or_7 (or_7_out, and_8_out, and_16_out);
  or or_8 (or_8_out, and_9_out, and_17_out);
  not not_3 (not_3_out, B1);
  and and_18 (and_18_out, or_8_out, ROT);
  and and_19 (and_19_out, or_7_out, ROT);
  not not_4 (not_4_out, not_3_out);
  and and_20 (and_20_out, not_3_out, or_1_out);
  and and_21 (and_21_out, not_3_out, or_2_out);
  and and_22 (and_22_out, not_3_out, or_3_out);
  and and_23 (and_23_out, not_3_out, or_4_out);
  and and_24 (and_24_out, not_3_out, or_5_out);
  and and_25 (and_25_out, not_3_out, or_6_out);
  and and_26 (and_26_out, not_3_out, or_7_out);
  and and_27 (and_27_out, not_3_out, or_8_out);
  and and_28 (and_28_out, not_4_out, and_19_out);
  and and_29 (and_29_out, not_4_out, and_18_out);
  and and_30 (and_30_out, not_4_out, or_1_out);
  and and_31 (and_31_out, not_4_out, or_2_out);
  and and_32 (and_32_out, not_4_out, or_3_out);
  and and_33 (and_33_out, not_4_out, or_4_out);
  and and_34 (and_34_out, not_4_out, or_5_out);
  and and_35 (and_35_out, not_4_out, or_6_out);
  or or_9 (or_9_out, and_20_out, and_28_out);
  or or_10 (or_10_out, and_21_out, and_29_out);
  or or_11 (or_11_out, and_22_out, and_30_out);
  or or_12 (or_12_out, and_23_out, and_31_out);
  or or_13 (or_13_out, and_24_out, and_32_out);
  or or_14 (or_14_out, and_25_out, and_33_out);
  or or_15 (or_15_out, and_26_out, and_34_out);
  or or_16 (or_16_out, and_27_out, and_35_out);
  not not_5 (not_5_out, B2);
  and and_36 (and_36_out, ROT, or_13_out);
  and and_37 (and_37_out, ROT, or_14_out);
  and and_38 (and_38_out, ROT, or_15_out);
  and and_39 (and_39_out, ROT, or_16_out);
  not not_6 (not_6_out, not_5_out);
  and and_40 (and_40_out, not_5_out, or_9_out);
  and and_41 (and_41_out, not_5_out, or_10_out);
  and and_42 (and_42_out, not_5_out, or_11_out);
  and and_43 (and_43_out, not_5_out, or_12_out);
  and and_44 (and_44_out, not_5_out, or_13_out);
  and and_45 (and_45_out, not_5_out, or_14_out);
  and and_46 (and_46_out, not_5_out, or_15_out);
  and and_47 (and_47_out, not_5_out, or_16_out);
  and and_48 (and_48_out, not_6_out, and_36_out);
  and and_49 (and_49_out, not_6_out, and_37_out);
  and and_50 (and_50_out, not_6_out, and_38_out);
  and and_51 (and_51_out, not_6_out, and_39_out);
  and and_52 (and_52_out, not_6_out, or_9_out);
  and and_53 (and_53_out, not_6_out, or_10_out);
  and and_54 (and_54_out, not_6_out, or_11_out);
  and and_55 (and_55_out, not_6_out, or_12_out);
  or or_17 (O7, and_40_out, and_48_out);
  or or_18 (O6, and_41_out, and_49_out);
  or or_19 (O5, and_42_out, and_50_out);
  or or_20 (O4, and_43_out, and_51_out);
  or or_21 (O3, and_44_out, and_52_out);
  or or_22 (O2, and_45_out, and_53_out);
  or or_23 (O1, and_46_out, and_54_out);
  or or_24 (O0, and_47_out, and_55_out);
endmodule

/* Test case:
A7 A6 A5 A4 A3 A2 A1 A0 B2 B1 B0 ROT O7 O6 O5 O4 O3 O2 O1 O0
1 0 1 1 0 1 1 0 0 1 0 0 0 0 1 0 1 1 0 1
1 1 1 0 0 0 0 0 0 0 0 1 1 1 1 0 0 0 0 0
1 0 0 1 0 1 1 1 0 0 1 0 0 1 0 0 1 0 1 1
1 0 0 1 0 1 0 1 1 1 0 1 0 1 0 1 0 1 1 0
1 0 0 1 0 0 0 1 1 0 0 0 0 0 0 0 1 0 0 1
1 1 1 1 1 0 0 0 0 0 1 0 0 1 1 1 1 1 0 0
0 1 0 0 0 1 0 0 0 0 1 1 0 0 1 0 0 0 1 0
0 1 1 0 0 1 1 0 1 1 1 1 1 1 0 0 1 1 0 0
0 1 0 0 1 0 1 1 0 0 0 1 0 1 0 0 1 0 1 1
1 1 1 0 1 0 0 0 0 1 0 1 0 0 1 1 1 0 1 0
0 1 0 0 0 1 1 1 0 0 1 0 0 0 1 0 0 0 1 1
1 1 1 0 1 1 1 1 1 0 1 1 0 1 1 1 1 1 1 1
1 1 1 1 1 1 0 1 0 0 0 1 1 1 1 1 1 1 0 1
1 1 0 0 0 0 0 0 1 1 0 0 0 0 0 0 0 0 1 1
0 1 1 0 1 0 1 0 0 0 1 1 0 0 1 1 0 1 0 1
1 0 1 0 1 1 0 0 1 1 0 0 0 0 0 0 0 0 1 0
1 0 1 1 1 1 0 0 0 0 0 0 1 0 1 1 1 1 0 0
1 0 1 0 0 1 0 1 1 0 0 0 0 0 0 0 1 0 1 0
0 1 0 0 1 0 1 0 1 1 1 1 1 0 0 1 0 1 0 0
1 0 1 0 0 0 0 1 1 1 1 0 0 0 0 0 0 0 0 1
0 0 1 1 0 1 0 0 1 0 0 0 0 0 0 0 0 0 1 1
0 0 1 0 1 1 0 1 1 1 0 0 0 0 0 0 0 0 0 0
0 0 0 0 1 0 1 0 0 0 1 1 0 0 0 0 0 1 0 1
0 0 1 1 1 1 1 1 1 1 0 1 1 1 1 1 1 1 0 0
0 1 1 0 1 0 0 1 1 0 1 1 0 1 0 0 1 0 1 1
0 1 0 1 1 1 0 1 1 0 0 0 0 0 0 0 0 1 0 1
1 1 1 0 0 1 0 0 1 0 0 0 0 0 0 0 1 1 1 0
1 0 1 0 0 0 0 0 0 0 0 0 1 0 1 0 0 0 0 0
1 0 0 0 0 0 1 1 1 0 1 1 0 0 0 1 1 1 0 0
0 0 1 1 1 0 0 1 0 1 1 1 0 0 1 0 0 1 1 1
0 1 1 0 0 1 0 0 1 1 1 1 1 1 0 0 1 0 0 0
1 0 0 0 0 0 0 1 1 0 1 0 0 0 0 0 0 1 0 0
1 1 1 1 1 1 1 1 1 1 1 0 0 0 0 0 0 0 0 1
0 1 1 0 0 0 0 0 1 0 1 0 0 0 0 0 0 0 1 1
0 1 1 0 0 1 0 0 1 1 0 0 0 0 0 0 0 0 0 1
1 0 1 0 1 0 1 0 0 0 1 1 0 1 0 1 0 1 0 1
0 0 1 1 0 0 0 1 0 0 1 1 1 0 0 1 1 0 0 0
1 0 1 0 1 1 0 0 1 0 1 1 0 1 1 0 0 1 0 1
1 1 0 1 1 1 1 1 0 1 1 0 0 0 0 1 1 0 1 1
0 0 0 1 0 1 1 0 1 1 1 1 0 0 1 0 1 1 0 0
0 0 1 0 0 1 0 0 0 1 0 0 0 0 0 0 1 0 0 1
1 0 0 1 0 0 1 1 1 1 1 0 0 0 0 0 0 0 0 1
0 0 1 0 0 1 1 0 1 0 0 0 0 0 0 0 0 0 1 0
1 1 1 0 0 0 1 0 1 1 0 1 1 0 0 0 1 0 1 1
1 0 1 0 1 0 0 0 1 0 0 1 1 0 0 0 1 0 1 0
1 1 0 1 1 1 1 0 0 1 1 1 1 1 0 1 1 0 1 1
1 1 1 1 1 0 0 0 0 1 0 1 0 0 1 1 1 1 1 0
0 1 1 0 0 0 1 0 0 0 0 0 0 1 1 0 0 0 1 0
0 0 0 1 1 0 1 0 0 1 1 1 0 1 0 0 0 0 1 1
1 0 0 1 0 0 0 1 1 0 0 1 0 0 0 1 1 0 0 1
1 0 1 0 1 1 0 0 1 1 0 1 1 0 1 1 0 0 1 0
0 1 0 1 0 1 0 0 0 0 1 0 0 0 1 0 1 0 1 0
1 0 0 0 0 1 0 0 0 1 1 0 0 0 0 1 0 0 0 0
0 1 0 1 0 1 0 0 1 0 1 1 1 0 1 0 0 0 1 0
1 1 1 0 0 0 1 1 0 0 0 0 1 1 1 0 0 0 1 1
0 0 0 1 1 1 0 1 1 0 1 1 1 1 1 0 1 0 0 0
0 0 0 0 0 1 1 1 0 0 1 1 1 0 0 0 0 0 1 1
0 0 0 0 0 1 0 1 0 1 0 0 0 0 0 0 0 0 0 1
1 0 1 1 1 0 0 0 0 1 1 1 0 0 0 1 0 1 1 1
1 1 1 0 0 1 1 1 0 0 1 1 1 1 1 1 0 0 1 1
1 0 1 1 1 1 0 0 0 0 1 0 0 1 0 1 1 1 1 0
1 1 1 0 0 0 0 1 0 1 1 1 0 0 1 1 1 1 0 0
1 0 0 0 1 0 0 0 0 0 1 1 0 1 0 0 0 1 0 0
1 0 1 1 0 0 0 1 0 0 1 1 1 1 0 1 1 0 0 0
0 0 0 1 0 0 0 1 0 0 0 0 0 0 0 1 0 0 0 1
1 0 1 1 0 1 0 1 0 1 1 1 1 0 1 1 0 1 1 0
0 0 1 1 0 1 1 0 1 0 1 0 0 0 0 0 0 0 0 1
0 1 1 0 1 0 0 0 1 1 1 1 1 1 0 1 0 0 0 0
1 1 0 0 1 0 0 0 0 0 1 0 0 1 1 0 0 1 0 0
0 1 0 0 0 0 1 0 1 0 0 1 0 0 1 0 0 1 0 0
1 1 0 1 0 1 1 1 0 1 0 1 1 1 1 1 0 1 0 1
0 1 1 1 1 0 1 0 0 1 1 1 0 1 0 0 1 1 1 1
1 0 1 0 0 1 0 0 1 0 0 1 0 1 0 0 1 0 1 0
1 1 1 1 0 0 1 0 0 1 0 0 0 0 1 1 1 1 0 0
0 0 0 0 1 1 1 1 1 1 0 1 0 0 1 1 1 1 0 0
1 1 0 0 0 1 0 1 0 0 0 0 1 1 0 0 0 1 0 1
1 0 1 1 0 0 0 1 0 0 0 1 1 0 1 1 0 0 0 1
1 0 1 1 0 1 1 1 1 1 0 0 0 0 0 0 0 0 1 0
0 0 0 0 0 1 0 0 1 0 0 0 0 0 0 0 0 0 0 0
1 1 0 0 0 1 1 0 1 1 1 1 1 0 0 0 1 1 0 1
0 0 1 1 1 1 1 0 0 0 1 0 0 0 0 1 1 1 1 1
1 0 1 1 1 0 1 0 1 0 1 1 1 1 0 1 0 1 0 1
0 0 0 1 1 1 0 1 1 0 1 1 1 1 1 0 1 0 0 0
0 0 0 1 1 0 1 0 0 0 0 1 0 0 0 1 1 0 1 0
1 1 1 0 1 1 0 0 0 0 1 0 0 1 1 1 0 1 1 0
0 1 0 0 0 1 1 0 1 0 0 1 0 1 1 0 0 1 0 0
1 0 1 0 0 1 0 0 0 1 0 0 0 0 1 0 1 0 0 1
1 1 0 1 0 0 1 0 1 1 1 0 0 0 0 0 0 0 0 1
0 1 1 0 0 0 1 1 1 1 1 1 1 1 0 0 0 1 1 0
0 1 0 1 1 1 0 0 1 1 0 0 0 0 0 0 0 0 0 1
1 0 1 1 0 0 1 1 0 0 0 1 1 0 1 1 0 0 1 1
0 1 1 0 1 0 1 0 0 1 1 0 0 0 0 0 1 1 0 1
0 1 1 0 0 1 1 0 0 1 1 0 0 0 0 0 1 1 0 0
1 0 1 0 1 0 0 1 1 1 1 0 0 0 0 0 0 0 0 1
1 0 1 1 0 0 0 1 0 0 0 1 1 0 1 1 0 0 0 1
1 1 1 1 1 0 1 0 0 0 0 1 1 1 1 1 1 0 1 0
1 1 0 1 0 0 1 1 0 0 1 0 0 1 1 0 1 0 0 1
0 1 0 1 0 1 1 1 0 1 0 1 1 1 0 1 0 1 0 1
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*/
