// Digital circuit barrel_shift_left.dig as structural Verilog
module barrel_shift_left (
  input  A0,
  input  A1,
  input  A2,
  input  A3,
  input  A4,
  input  A5,
  input  A6,
  input  A7,
  input  B0,
  input  B1,
  input  B2,
  input  ROT,
  output O0,
  output O1,
  output O2,
  output O3,
  output O4,
  output O5,
  output O6,
  output O7
);

  barell_shift_right barell_shift_right_1 (
    .A0(A7), .A1(A6), .A2(A5), .A3(A4), .A4(A3), .A5(A2), .A6(A1), .A7(A0), .B0(B0), .B1(B1), .B2(B2),
    .ROT(ROT), .O0(O7), .O1(O6), .O2(O5), .O3(O4), .O4(O3), .O5(O2), .O6(O1), .O7(O0));
endmodule

/* Test case:
A7 A6 A5 A4 A3 A2 A1 A0 B2 B1 B0 ROT O7 O6 O5 O4 O3 O2 O1 O0
1 0 1 0 0 0 0 1 0 0 1 1 0 1 0 0 0 0 1 1
1 0 0 0 0 1 0 0 0 1 0 1 0 0 0 1 0 0 1 0
1 1 1 1 1 1 0 0 0 1 0 0 1 1 1 1 0 0 0 0
1 1 1 1 1 0 0 1 1 0 0 1 1 0 0 1 1 1 1 1
1 0 1 0 1 0 1 1 1 0 1 0 0 1 1 0 0 0 0 0
1 1 1 1 1 1 1 0 1 0 1 0 1 1 0 0 0 0 0 0
1 0 1 1 0 0 1 0 0 1 1 0 1 0 0 1 0 0 0 0
0 1 1 0 1 0 0 0 0 1 1 0 0 1 0 0 0 0 0 0
0 1 0 1 1 0 1 0 0 0 1 0 1 0 1 1 0 1 0 0
1 1 0 0 0 0 1 0 0 0 1 1 1 0 0 0 0 1 0 1
0 1 1 1 0 0 1 1 0 0 1 1 1 1 1 0 0 1 1 0
1 0 1 1 1 1 0 1 0 0 1 1 0 1 1 1 1 0 1 1
1 0 1 1 1 0 1 0 1 0 1 0 0 1 0 0 0 0 0 0
1 1 0 1 0 1 1 0 0 0 1 1 1 0 1 0 1 1 0 1
0 0 0 1 1 0 1 1 1 1 1 0 1 0 0 0 0 0 0 0
0 0 0 1 0 0 1 0 0 1 1 0 1 0 0 1 0 0 0 0
1 1 0 1 0 1 1 0 0 0 1 1 1 0 1 0 1 1 0 1
0 0 1 1 1 1 1 1 1 0 0 0 1 1 1 1 0 0 0 0
0 0 0 1 0 0 1 0 0 0 1 0 0 0 1 0 0 1 0 0
0 1 1 1 1 1 0 1 0 0 1 1 1 1 1 1 1 0 1 0
1 0 1 0 0 0 1 0 1 0 0 1 0 0 1 0 1 0 1 0
0 1 1 0 1 1 0 1 0 1 1 0 0 1 1 0 1 0 0 0
1 0 0 1 0 0 1 0 0 1 1 1 1 0 0 1 0 1 0 0
1 1 1 1 1 1 1 1 1 1 1 1 1 1 1 1 1 1 1 1
1 1 1 1 0 0 0 1 1 1 1 0 1 0 0 0 0 0 0 0
0 0 1 1 1 1 0 1 1 0 0 1 1 1 0 1 0 0 1 1
0 1 0 0 1 1 1 0 0 1 1 0 0 1 1 1 0 0 0 0
1 0 0 0 1 0 1 1 1 0 0 1 1 0 1 1 1 0 0 0
0 0 0 1 0 1 1 0 1 1 0 1 1 0 0 0 0 1 0 1
0 0 0 1 0 0 1 0 0 1 0 0 0 1 0 0 1 0 0 0
0 0 0 0 1 0 0 0 1 1 0 0 0 0 0 0 0 0 0 0
0 1 0 0 1 0 0 0 0 1 1 0 0 1 0 0 0 0 0 0
0 1 1 0 1 0 1 1 0 1 1 0 0 1 0 1 1 0 0 0
0 1 1 1 1 0 1 1 0 1 1 1 1 1 0 1 1 0 1 1
1 1 1 0 1 0 0 0 0 0 1 0 1 1 0 1 0 0 0 0
1 1 1 1 0 0 1 1 0 1 0 1 1 1 0 0 1 1 1 1
1 1 0 0 1 1 0 1 0 0 0 0 1 1 0 0 1 1 0 1
0 1 0 0 1 0 0 1 0 0 1 1 1 0 0 1 0 0 1 0
1 1 1 0 1 0 1 0 0 1 1 0 0 1 0 1 0 0 0 0
0 1 0 1 1 1 1 0 0 1 1 0 1 1 1 1 0 0 0 0
1 0 0 1 1 1 1 0 0 1 0 1 0 1 1 1 1 0 1 0
0 0 1 1 0 0 0 1 0 1 0 0 1 1 0 0 0 1 0 0
0 1 0 1 0 0 0 1 1 0 1 1 0 0 1 0 1 0 1 0
1 1 0 0 0 0 0 1 0 0 0 1 1 1 0 0 0 0 0 1
1 1 1 0 1 0 1 1 1 0 0 0 1 0 1 1 0 0 0 0
1 1 0 0 0 0 1 0 1 1 1 0 0 0 0 0 0 0 0 0
0 0 0 0 1 1 1 1 0 1 0 1 0 0 1 1 1 1 0 0
1 0 0 1 1 1 1 0 1 1 1 0 0 0 0 0 0 0 0 0
1 0 0 1 1 0 0 1 1 0 1 1 0 0 1 1 0 0 1 1
1 1 1 0 0 0 1 1 1 1 0 1 1 1 1 1 1 0 0 0
1 1 1 1 0 1 1 1 1 1 1 1 1 1 1 1 1 0 1 1
0 1 0 0 0 1 1 0 1 1 0 0 1 0 0 0 0 0 0 0
1 0 1 1 0 0 1 0 1 0 1 1 0 1 0 1 0 1 1 0
0 0 0 1 0 1 1 0 0 0 1 1 0 0 1 0 1 1 0 0
1 1 0 0 1 0 1 1 1 0 1 1 0 1 1 1 1 0 0 1
0 0 1 0 1 1 1 0 0 0 1 0 0 1 0 1 1 1 0 0
1 0 1 0 1 0 0 1 0 1 1 1 0 1 0 0 1 1 0 1
0 1 0 1 0 1 1 1 1 1 1 0 1 0 0 0 0 0 0 0
1 1 1 1 1 0 1 0 1 1 0 1 1 0 1 1 1 1 1 0
1 0 0 0 1 0 0 1 0 1 0 0 0 0 1 0 0 1 0 0
1 1 0 1 0 0 0 0 0 0 0 1 1 1 0 1 0 0 0 0
0 0 1 1 1 0 1 1 0 0 0 1 0 0 1 1 1 0 1 1
0 0 0 1 1 1 0 0 0 0 1 0 0 0 1 1 1 0 0 0
0 1 1 1 1 1 1 0 1 0 0 0 1 1 1 0 0 0 0 0
0 0 1 1 1 0 1 0 0 1 1 1 1 1 0 1 0 0 0 1
1 0 1 1 1 1 0 0 1 0 1 1 1 0 0 1 0 1 1 1
1 0 0 0 1 0 1 1 0 1 1 1 0 1 0 1 1 1 0 0
1 0 0 1 0 1 0 1 0 0 1 1 0 0 1 0 1 0 1 1
0 0 0 0 1 0 1 0 0 0 0 1 0 0 0 0 1 0 1 0
0 1 0 1 1 0 0 0 1 1 0 0 0 0 0 0 0 0 0 0
1 1 1 0 1 1 1 0 0 1 1 0 0 1 1 1 0 0 0 0
0 1 0 1 1 1 0 0 0 1 0 1 0 1 1 1 0 0 0 1
0 0 0 0 0 0 1 1 1 1 0 1 1 1 0 0 0 0 0 0
1 1 1 0 0 1 0 0 1 0 1 1 1 0 0 1 1 1 0 0
1 1 0 0 0 0 0 0 0 1 1 0 0 0 0 0 0 0 0 0
1 0 0 1 0 1 1 0 0 1 1 0 1 0 1 1 0 0 0 0
0 0 1 1 0 0 1 1 1 1 0 0 1 1 0 0 0 0 0 0
0 0 0 1 1 1 1 0 1 1 0 1 1 0 0 0 0 1 1 1
1 1 0 1 1 1 1 0 0 1 0 1 0 1 1 1 1 0 1 1
1 0 1 0 0 0 1 0 0 0 1 1 0 1 0 0 0 1 0 1
0 0 0 0 0 1 0 0 0 0 1 0 0 0 0 0 1 0 0 0
1 0 1 0 1 1 0 1 0 0 1 1 0 1 0 1 1 0 1 1
1 0 0 1 1 0 0 0 1 1 0 1 0 0 1 0 0 1 1 0
0 1 0 0 1 1 0 1 1 0 0 1 1 1 0 1 0 1 0 0
0 0 0 0 1 0 1 0 0 1 0 1 0 0 1 0 1 0 0 0
1 0 1 0 0 0 1 0 1 0 0 0 0 0 1 0 0 0 0 0
0 1 0 0 0 1 0 0 1 1 0 0 0 0 0 0 0 0 0 0
0 0 1 1 0 0 1 0 1 1 1 0 0 0 0 0 0 0 0 0
1 1 0 0 0 0 0 1 0 0 0 0 1 1 0 0 0 0 0 1
1 1 1 0 1 1 1 1 1 1 1 1 1 1 1 1 0 1 1 1
0 1 1 0 0 0 1 0 1 0 1 0 0 1 0 0 0 0 0 0
1 1 0 0 1 1 0 1 0 1 1 1 0 1 1 0 1 1 1 0
0 1 1 0 1 0 1 1 0 1 0 0 1 0 1 0 1 1 0 0
0 1 0 1 1 0 1 1 0 0 1 1 1 0 1 1 0 1 1 0
0 1 0 0 0 0 0 0 1 1 1 0 0 0 0 0 0 0 0 0
1 0 1 0 1 0 1 1 0 0 0 0 1 0 1 0 1 0 1 1
0 0 1 0 0 0 0 1 1 0 1 1 0 0 1 0 0 1 0 0
1 0 1 0 1 1 1 1 1 1 0 0 1 1 0 0 0 0 0 0
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*/
