// Digital circuit demo.dig as structural Verilog
module demo (
  input  [6:0] in_1,
  input  [6:0] in_2,
  input  in_3,
  input  in_4,
  input  [3:0] in_5,
  output out_6,
  output [6:0] out_7,
  output out_8,
  output [6:0] out_9,
  output out_10,
  output [14:0] out_11,
  output out_12,
  output out_13,
  output out_14,
  output out_15,
  output out_16,
  output out_17,
  output out_18,
  output out_19,
  output F_OF,
  output F_Z,
  output F_LZ,
  output F_GZ,
  output F_PAR,
  output F_ERR
);

  alu alu_1 (
    .A0(in_1[0]), .A1(in_1[1]), .A2(in_1[2]), .A3(in_1[3]), .A4(in_1[4]), .A5(in_1[5]), .A6(in_1[6]),
    .A7(in_3), .B0(in_2[0]), .B1(in_2[1]), .B2(in_2[2]), .B3(in_2[3]), .B4(in_2[4]), .B5(in_2[5]),
    .B6(in_2[6]), .B7(in_4), .OPT0(in_5[0]), .OPT1(in_5[1]), .OPT2(in_5[2]), .OPT3(in_5[3]), .O0(out_7[0]),
    .O1(out_7[1]), .O2(out_7[2]), .O3(out_7[3]), .O4(out_7[4]), .O5(out_7[5]), .O6(out_7[6]), .O7(out_6),
    .P0(out_9[0]), .P1(out_9[1]), .P2(out_9[2]), .P3(out_9[3]), .P4(out_9[4]), .P5(out_9[5]), .P6(out_9[6]),
    .P7(out_8), .F_OF(F_OF), .F_Z(F_Z), .F_LZ(F_LZ), .F_GZ(F_GZ), .F_PAR(F_PAR), .F_DIV0(F_ERR));

  assign out_10 = out_8;
  assign out_11 = {out_9, out_6, out_7};
  assign out_12 = out_7[0];
  assign out_13 = out_7[1];
  assign out_14 = out_7[2];
  assign out_15 = out_7[3];
  assign out_16 = out_7[4];
  assign out_17 = out_7[5];
  assign out_18 = out_7[6];
  assign out_19 = out_6;

  // Notes on the sheet:
  //   IN1
  //   IN2
  //   OPT
  //   OPT CODES:
  //   0 ADD
  //   1 SUB
  //   2 MUL
  //   3 DIVMOD
  //   4 SHL
  //   5 ROTL
  //   6 SHR
  //   7 ROTR
  //   8 AND
  //   9 OR
  //   10 XOR
  //   11 NOT
  //   12 PASS
  //   13 COMPL
  //   14 INC
  //   15 DEC
  //   8 bit out
  //   16 bit out
  //   Binary out
  //   Flags
  //   LS
  //   MS
endmodule
