// Digital circuit dividor.dig as structural Verilog
module dividor (
  input  A0,
  input  B0,
  input  A1,
  input  B1,
  input  A2,
  input  B2,
  input  A3,
  input  B3,
  input  A4,
  input  B4,
  input  A5,
  input  B5,
  input  A6,
  input  B6,
  input  A7,
  input  B7,
  output o6,
  output o5,
  output o4,
  output o3,
  output o2,
  output o1,
  output o0,
  output m0,
  output m1,
  output m2,
  output m3,
  output m4,
  output m5,
  output m6,
  output sgn,
  output div0
);

  wire and_1_out, and_2_out, and_3_out, and_4_out, and_5_out, and_6_out, and_7_out, and_8_out, and_9_out,
       and_10_out, and_11_out, and_12_out, and_13_out, and_14_out, and_15_out, and_16_out, and_17_out,
       and_18_out, and_19_out, and_20_out, and_21_out, and_22_out, and_23_out, and_24_out, and_25_out,
       and_26_out, and_27_out, and_28_out, and_29_out, and_30_out, and_31_out, and_32_out, and_33_out,
       and_34_out, and_35_out, and_36_out, and_37_out, and_38_out, and_39_out, and_40_out, and_41_out,
       and_42_out, and_43_out, and_44_out, and_45_out, and_46_out, and_47_out, and_48_out, and_49_out,
       and_50_out, and_51_out, and_52_out, and_53_out, and_54_out, and_55_out, and_56_out, and_57_out,
       and_58_out, and_59_out, and_60_out, and_61_out, and_62_out, and_63_out, and_64_out, and_65_out,
       and_66_out, and_67_out, and_68_out, and_69_out, and_70_out, and_71_out, and_72_out, and_73_out,
       and_74_out, and_75_out, and_76_out, and_77_out, and_78_out, and_79_out, and_80_out, and_81_out,
       and_82_out, and_83_out, and_84_out, and_85_out, and_86_out, and_87_out, and_88_out, and_89_out,
       and_90_out, and_91_out, and_92_out, and_93_out, and_94_out, and_95_out, and_96_out, and_97_out,
       and_98_out, or_1_out, or_2_out, or_3_out, or_4_out, or_5_out, or_6_out, or_7_out, or_8_out, or_9_out,
       or_10_out, or_11_out, or_12_out, or_13_out, or_14_out, or_15_out, or_16_out, or_17_out, or_18_out,
       or_19_out, or_20_out, or_21_out, or_22_out, or_23_out, or_24_out, or_25_out, or_26_out, or_27_out,
       or_28_out, or_29_out, or_30_out, or_31_out, or_32_out, or_33_out, or_34_out, or_35_out, or_36_out,
       or_37_out, or_38_out, or_39_out, or_40_out, or_41_out, or_42_out, or_43_out, or_44_out, or_45_out,
       or_46_out, or_47_out, or_48_out, or_49_out, or_50_out, or_51_out, or_52_out, or_53_out, or_54_out,
       or_55_out, or_56_out, signed_8bit_adder_1_o0, signed_8bit_adder_1_o1, signed_8bit_adder_1_o2,
       signed_8bit_adder_1_o3, signed_8bit_adder_1_o4, signed_8bit_adder_1_o5, signed_8bit_adder_1_o6,
       signed_8bit_adder_1_sgn, signed_8bit_adder_2_o0, signed_8bit_adder_2_o1, signed_8bit_adder_2_o2,
       signed_8bit_adder_2_o3, signed_8bit_adder_2_o4, signed_8bit_adder_2_o5, signed_8bit_adder_2_o6,
       signed_8bit_adder_2_sgn, signed_8bit_adder_3_o0, signed_8bit_adder_3_o1, signed_8bit_adder_3_o2,
       signed_8bit_adder_3_o3, signed_8bit_adder_3_o4, signed_8bit_adder_3_o5, signed_8bit_adder_3_o6,
       signed_8bit_adder_3_sgn, signed_8bit_adder_4_o0, signed_8bit_adder_4_o1, signed_8bit_adder_4_o2,
       signed_8bit_adder_4_o3, signed_8bit_adder_4_o4, signed_8bit_adder_4_o5, signed_8bit_adder_4_o6,
       signed_8bit_adder_4_sgn, signed_8bit_adder_5_o0, signed_8bit_adder_5_o1, signed_8bit_adder_5_o2,
       signed_8bit_adder_5_o3, signed_8bit_adder_5_o4, signed_8bit_adder_5_o5, signed_8bit_adder_5_o6,
       signed_8bit_adder_5_sgn, signed_8bit_adder_6_o0, signed_8bit_adder_6_o1, signed_8bit_adder_6_o2,
       signed_8bit_adder_6_o3, signed_8bit_adder_6_o4, signed_8bit_adder_6_o5, signed_8bit_adder_6_o6,
       signed_8bit_adder_6_sgn, signed_8bit_adder_7_o0, signed_8bit_adder_7_o1, signed_8bit_adder_7_o2,
       signed_8bit_adder_7_o3, signed_8bit_adder_7_o4, signed_8bit_adder_7_o5, signed_8bit_adder_7_o6,
       signed_8bit_adder_7_sgn;

  xor xor_1 (sgn, B7, A7);
  or or_1 (or_1_out, B5, B6);
  or or_2 (or_2_out, B1, B2, B3, B4, or_1_out);
  or or_3 (or_3_out, B0, B1, B2, B3);
  or or_4 (or_4_out, or_2_out, signed_8bit_adder_1_sgn);
  nor nor_1 (div0, or_3_out, or_5_out);
  signed_8bit_adder signed_8bit_adder_1 (
    .A0(A0), .B0(1'b0), .A1(A1), .B1(1'b0), .A2(A2), .B2(1'b0), .A3(A3), .B3(1'b0), .A4(A4), .B4(1'b0),
    .A5(A5), .B5(1'b0), .A6(A6), .B6(B0), .A7(1'b0), .B7(1'b1), .o0(signed_8bit_adder_1_o0),
    .o1(signed_8bit_adder_1_o1), .o2(signed_8bit_adder_1_o2), .o3(signed_8bit_adder_1_o3),
    .o4(signed_8bit_adder_1_o4), .o5(signed_8bit_adder_1_o5), .o6(signed_8bit_adder_1_o6),
    .sgn(signed_8bit_adder_1_sgn));  // open: o7
  or or_5 (or_5_out, B4, B5, B6);
  not not_1 (o6, or_4_out);
  and and_1 (and_1_out, or_4_out, A0);
  and and_2 (and_2_out, or_4_out, A1);
  and and_3 (and_3_out, or_4_out, A2);
  and and_4 (and_4_out, or_4_out, A3);
  and and_5 (and_5_out, or_4_out, A4);
  and and_6 (and_6_out, or_4_out, A5);
  and and_7 (and_7_out, or_4_out, A6);
  and and_8 (and_8_out, o6, signed_8bit_adder_1_o0);
  and and_9 (and_9_out, o6, signed_8bit_adder_1_o1);
  and and_10 (and_10_out, o6, signed_8bit_adder_1_o2);
  and and_11 (and_11_out, o6, signed_8bit_adder_1_o3);
  and and_12 (and_12_out, o6, signed_8bit_adder_1_o4);
  and and_13 (and_13_out, o6, signed_8bit_adder_1_o5);
  and and_14 (and_14_out, o6, signed_8bit_adder_1_o6);
  or or_6 (or_6_out, and_1_out, and_8_out);
  or or_7 (or_7_out, and_2_out, and_9_out);
  or or_8 (or_8_out, and_3_out, and_10_out);
  or or_9 (or_9_out, and_4_out, and_11_out);
  or or_10 (or_10_out, and_5_out, and_12_out);
  or or_11 (or_11_out, and_6_out, and_13_out);
  or or_12 (or_12_out, and_7_out, and_14_out);
  or or_13 (or_13_out, B2, B3, B4, B5, B6);
  or or_14 (or_14_out, or_13_out, signed_8bit_adder_2_sgn);
  signed_8bit_adder signed_8bit_adder_2 (
    .A0(or_6_out), .B0(1'b0), .A1(or_7_out), .B1(1'b0), .A2(or_8_out), .B2(1'b0), .A3(or_9_out), .B3(1'b0),
    .A4(or_10_out), .B4(1'b0), .A5(or_11_out), .B5(B0), .A6(or_12_out), .B6(B1), .A7(1'b0), .B7(1'b1),
    .o0(signed_8bit_adder_2_o0), .o1(signed_8bit_adder_2_o1), .o2(signed_8bit_adder_2_o2),
    .o3(signed_8bit_adder_2_o3), .o4(signed_8bit_adder_2_o4), .o5(signed_8bit_adder_2_o5),
    .o6(signed_8bit_adder_2_o6), .sgn(signed_8bit_adder_2_sgn));  // open: o7
  not not_2 (o5, or_14_out);
  and and_15 (and_15_out, or_14_out, or_6_out);
  and and_16 (and_16_out, or_14_out, or_7_out);
  and and_17 (and_17_out, or_14_out, or_8_out);
  and and_18 (and_18_out, or_14_out, or_9_out);
  and and_19 (and_19_out, or_14_out, or_10_out);
  and and_20 (and_20_out, or_14_out, or_11_out);
  and and_21 (and_21_out, or_14_out, or_12_out);
  and and_22 (and_22_out, o5, signed_8bit_adder_2_o0);
  and and_23 (and_23_out, o5, signed_8bit_adder_2_o1);
  and and_24 (and_24_out, o5, signed_8bit_adder_2_o2);
  and and_25 (and_25_out, o5, signed_8bit_adder_2_o3);
  and and_26 (and_26_out, o5, signed_8bit_adder_2_o4);
  and and_27 (and_27_out, o5, signed_8bit_adder_2_o5);
  and and_28 (and_28_out, o5, signed_8bit_adder_2_o6);
  or or_15 (or_15_out, and_15_out, and_22_out);
  or or_16 (or_16_out, and_16_out, and_23_out);
  or or_17 (or_17_out, and_17_out, and_24_out);
  or or_18 (or_18_out, and_18_out, and_25_out);
  or or_19 (or_19_out, and_19_out, and_26_out);
  or or_20 (or_20_out, and_20_out, and_27_out);
  or or_21 (or_21_out, and_21_out, and_28_out);
  or or_22 (or_22_out, B3, B4, B5, B6);
  or or_23 (or_23_out, or_22_out, signed_8bit_adder_3_sgn);
  signed_8bit_adder signed_8bit_adder_3 (
    .A0(or_15_out), .B0(1'b0), .A1(or_16_out), .B1(1'b0), .A2(or_17_out), .B2(1'b0), .A3(or_18_out),
    .B3(1'b0), .A4(or_19_out), .B4(B0), .A5(or_20_out), .B5(B1), .A6(or_21_out), .B6(B2), .A7(1'b0),
    .B7(1'b1), .o0(signed_8bit_adder_3_o0), .o1(signed_8bit_adder_3_o1), .o2(signed_8bit_adder_3_o2),
    .o3(signed_8bit_adder_3_o3), .o4(signed_8bit_adder_3_o4), .o5(signed_8bit_adder_3_o5),
    .o6(signed_8bit_adder_3_o6), .sgn(signed_8bit_adder_3_sgn));  // open: o7
  not not_3 (o4, or_23_out);
  and and_29 (and_29_out, or_23_out, or_15_out);
  and and_30 (and_30_out, or_23_out, or_16_out);
  and and_31 (and_31_out, or_23_out, or_17_out);
  and and_32 (and_32_out, or_23_out, or_18_out);
  and and_33 (and_33_out, or_23_out, or_19_out);
  and and_34 (and_34_out, or_23_out, or_20_out);
  and and_35 (and_35_out, or_23_out, or_21_out);
  and and_36 (and_36_out, o4, signed_8bit_adder_3_o0);
  and and_37 (and_37_out, o4, signed_8bit_adder_3_o1);
  and and_38 (and_38_out, o4, signed_8bit_adder_3_o2);
  and and_39 (and_39_out, o4, signed_8bit_adder_3_o3);
  and and_40 (and_40_out, o4, signed_8bit_adder_3_o4);
  and and_41 (and_41_out, o4, signed_8bit_adder_3_o5);
  and and_42 (and_42_out, o4, signed_8bit_adder_3_o6);
  or or_24 (or_24_out, and_29_out, and_36_out);
  or or_25 (or_25_out, and_30_out, and_37_out);
  or or_26 (or_26_out, and_31_out, and_38_out);
  or or_27 (or_27_out, and_32_out, and_39_out);
  or or_28 (or_28_out, and_33_out, and_40_out);
  or or_29 (or_29_out, and_34_out, and_41_out);
  or or_30 (or_30_out, and_35_out, and_42_out);
  or or_31 (or_31_out, B4, B5, B6);
  or or_32 (or_32_out, or_31_out, signed_8bit_adder_4_sgn);
  signed_8bit_adder signed_8bit_adder_4 (
    .A0(or_24_out), .B0(1'b0), .A1(or_25_out), .B1(1'b0), .A2(or_26_out), .B2(1'b0), .A3(or_27_out), .B3(B0),
    .A4(or_28_out), .B4(B1), .A5(or_29_out), .B5(B2), .A6(or_30_out), .B6(B3), .A7(1'b0), .B7(1'b1),
    .o0(signed_8bit_adder_4_o0), .o1(signed_8bit_adder_4_o1), .o2(signed_8bit_adder_4_o2),
    .o3(signed_8bit_adder_4_o3), .o4(signed_8bit_adder_4_o4), .o5(signed_8bit_adder_4_o5),
    .o6(signed_8bit_adder_4_o6), .sgn(signed_8bit_adder_4_sgn));  // open: o7
  not not_4 (o3, or_32_out);
  and and_43 (and_43_out, or_32_out, or_24_out);
  and and_44 (and_44_out, or_32_out, or_25_out);
  and and_45 (and_45_out, or_32_out, or_26_out);
  and and_46 (and_46_out, or_32_out, or_27_out);
  and and_47 (and_47_out, or_32_out, or_28_out);
  and and_48 (and_48_out, or_32_out, or_29_out);
  and and_49 (and_49_out, or_32_out, or_30_out);
  and and_50 (and_50_out, o3, signed_8bit_adder_4_o0);
  and and_51 (and_51_out, o3, signed_8bit_adder_4_o1);
  and and_52 (and_52_out, o3, signed_8bit_adder_4_o2);
  and and_53 (and_53_out, o3, signed_8bit_adder_4_o3);
  and and_54 (and_54_out, o3, signed_8bit_adder_4_o4);
  and and_55 (and_55_out, o3, signed_8bit_adder_4_o5);
  and and_56 (and_56_out, o3, signed_8bit_adder_4_o6);
  or or_33 (or_33_out, and_43_out, and_50_out);
  or or_34 (or_34_out, and_44_out, and_51_out);
  or or_35 (or_35_out, and_45_out, and_52_out);
  or or_36 (or_36_out, and_46_out, and_53_out);
  or or_37 (or_37_out, and_47_out, and_54_out);
  or or_38 (or_38_out, and_48_out, and_55_out);
  or or_39 (or_39_out, and_49_out, and_56_out);
  or or_40 (or_40_out, B5, B6);
  or or_41 (or_41_out, or_40_out, signed_8bit_adder_5_sgn);
  signed_8bit_adder signed_8bit_adder_5 (
    .A0(or_33_out), .B0(1'b0), .A1(or_34_out), .B1(1'b0), .A2(or_35_out), .B2(B0), .A3(or_36_out), .B3(B1),
    .A4(or_37_out), .B4(B2), .A5(or_38_out), .B5(B3), .A6(or_39_out), .B6(B4), .A7(1'b0), .B7(1'b1),
    .o0(signed_8bit_adder_5_o0), .o1(signed_8bit_adder_5_o1), .o2(signed_8bit_adder_5_o2),
    .o3(signed_8bit_adder_5_o3), .o4(signed_8bit_adder_5_o4), .o5(signed_8bit_adder_5_o5),
    .o6(signed_8bit_adder_5_o6), .sgn(signed_8bit_adder_5_sgn));  // open: o7
  not not_5 (o2, or_41_out);
  and and_57 (and_57_out, or_41_out, or_33_out);
  and and_58 (and_58_out, or_41_out, or_34_out);
  and and_59 (and_59_out, or_41_out, or_35_out);
  and and_60 (and_60_out, or_41_out, or_36_out);
  and and_61 (and_61_out, or_41_out, or_37_out);
  and and_62 (and_62_out, or_41_out, or_38_out);
  and and_63 (and_63_out, or_41_out, or_39_out);
  and and_64 (and_64_out, o2, signed_8bit_adder_5_o0);
  and and_65 (and_65_out, o2, signed_8bit_adder_5_o1);
  and and_66 (and_66_out, o2, signed_8bit_adder_5_o2);
  and and_67 (and_67_out, o2, signed_8bit_adder_5_o3);
  and and_68 (and_68_out, o2, signed_8bit_adder_5_o4);
  and and_69 (and_69_out, o2, signed_8bit_adder_5_o5);
  and and_70 (and_70_out, o2, signed_8bit_adder_5_o6);
  or or_42 (or_42_out, and_57_out, and_64_out);
  or or_43 (or_43_out, and_58_out, and_65_out);
  or or_44 (or_44_out, and_59_out, and_66_out);
  or or_45 (or_45_out, and_60_out, and_67_out);
  or or_46 (or_46_out, and_61_out, and_68_out);
  or or_47 (or_47_out, and_62_out, and_69_out);
  or or_48 (or_48_out, and_63_out, and_70_out);
  or or_49 (or_49_out, B6, signed_8bit_adder_6_sgn);
  signed_8bit_adder signed_8bit_adder_6 (
    .A0(or_42_out), .B0(1'b0), .A1(or_43_out), .B1(B0), .A2(or_44_out), .B2(B1), .A3(or_45_out), .B3(B2),
    .A4(or_46_out), .B4(B3), .A5(or_47_out), .B5(B4), .A6(or_48_out), .B6(B5), .A7(1'b0), .B7(1'b1),
    .o0(signed_8bit_adder_6_o0), .o1(signed_8bit_adder_6_o1), .o2(signed_8bit_adder_6_o2),
    .o3(signed_8bit_adder_6_o3), .o4(signed_8bit_adder_6_o4), .o5(signed_8bit_adder_6_o5),
    .o6(signed_8bit_adder_6_o6), .sgn(signed_8bit_adder_6_sgn));  // open: o7
  not not_6 (o1, or_49_out);
  and and_71 (and_71_out, or_49_out, or_42_out);
  and and_72 (and_72_out, or_49_out, or_43_out);
  and and_73 (and_73_out, or_49_out, or_44_out);
  and and_74 (and_74_out, or_49_out, or_45_out);
  and and_75 (and_75_out, or_49_out, or_46_out);
  and and_76 (and_76_out, or_49_out, or_47_out);
  and and_77 (and_77_out, or_49_out, or_48_out);
  and and_78 (and_78_out, o1, signed_8bit_adder_6_o0);
  and and_79 (and_79_out, o1, signed_8bit_adder_6_o1);
  and and_80 (and_80_out, o1, signed_8bit_adder_6_o2);
  and and_81 (and_81_out, o1, signed_8bit_adder_6_o3);
  and and_82 (and_82_out, o1, signed_8bit_adder_6_o4);
  and and_83 (and_83_out, o1, signed_8bit_adder_6_o5);
  and and_84 (and_84_out, o1, signed_8bit_adder_6_o6);
  or or_50 (or_50_out, and_71_out, and_78_out);
  or or_51 (or_51_out, and_72_out, and_79_out);
  or or_52 (or_52_out, and_73_out, and_80_out);
  or or_53 (or_53_out, and_74_out, and_81_out);
  or or_54 (or_54_out, and_75_out, and_82_out);
  or or_55 (or_55_out, and_76_out, and_83_out);
  or or_56 (or_56_out, and_77_out, and_84_out);
  signed_8bit_adder signed_8bit_adder_7 (
    .A0(or_50_out), .B0(B0), .A1(or_51_out), .B1(B1), .A2(or_52_out), .B2(B2), .A3(or_53_out), .B3(B3),
    .A4(or_54_out), .B4(B4), .A5(or_55_out), .B5(B5), .A6(or_56_out), .B6(B6), .A7(1'b0), .B7(1'b1),
    .o0(signed_8bit_adder_7_o0), .o1(signed_8bit_adder_7_o1), .o2(signed_8bit_adder_7_o2),
    .o3(signed_8bit_adder_7_o3), .o4(signed_8bit_adder_7_o4), .o5(signed_8bit_adder_7_o5),
    .o6(signed_8bit_adder_7_o6), .sgn(signed_8bit_adder_7_sgn));  // open: o7
  not not_7 (o0, signed_8bit_adder_7_sgn);
  and and_85 (and_85_out, signed_8bit_adder_7_sgn, or_50_out);
  and and_86 (and_86_out, signed_8bit_adder_7_sgn, or_51_out);
  and and_87 (and_87_out, signed_8bit_adder_7_sgn, or_52_out);
  and and_88 (and_88_out, signed_8bit_adder_7_sgn, or_53_out);
  and and_89 (and_89_out, signed_8bit_adder_7_sgn, or_54_out);
  and and_90 (and_90_out, signed_8bit_adder_7_sgn, or_55_out);
  and and_91 (and_91_out, signed_8bit_adder_7_sgn, or_56_out);
  and and_92 (and_92_out, o0, signed_8bit_adder_7_o0);
  and and_93 (and_93_out, o0, signed_8bit_adder_7_o1);
  and and_94 (and_94_out, o0, signed_8bit_adder_7_o2);
  and and_95 (and_95_out, o0, signed_8bit_adder_7_o3);
  and and_96 (and_96_out, o0, signed_8bit_adder_7_o4);
  and and_97 (and_97_out, o0, signed_8bit_adder_7_o5);
  and and_98 (and_98_out, o0, signed_8bit_adder_7_o6);
  or or_57 (m0, and_85_out, and_92_out);
  or or_58 (m1, and_86_out, and_93_out);
  or or_59 (m2, and_87_out, and_94_out);
  or or_60 (m3, and_88_out, and_95_out);
  or or_61 (m4, and_89_out, and_96_out);
  or or_62 (m5, and_90_out, and_97_out);
  or or_63 (m6, and_91_out, and_98_out);
endmodule

/* Test case:
A7 A6 A5 A4 A3 A2 A1 A0 B7 B6 B5 B4 B3 B2 B1 B0 sgn o6 o5 o4 o3 o2 o1 o0 m6 m5 m4 m3 m2 m1 m0
0 1 1 1 1 0 1 0 0 1 1 1 1 1 1 0 0 0 0 0 0 0 0 0 1 1 1 1 0 1 0
0 0 0 1 1 1 0 0 0 0 0 0 1 0 0 1 0 0 0 0 0 0 1 1 0 0 0 0 0 0 1
0 0 0 1 0 1 1 1 0 0 0 0 0 1 1 0 0 0 0 0 0 0 1 1 0 0 0 0 1 0 1
0 0 0 0 0 0 1 0 0 0 1 1 1 0 1 1 0 0 0 0 0 0 0 0 0 0 0 0 0 1 0
0 0 1 1 1 1 1 0 0 0 1 1 0 1 0 0 0 0 0 0 0 0 0 1 0 0 0 1 0 1 0
0 1 1 1 0 1 0 1 0 1 0 1 1 1 0 0 0 0 0 0 0 0 0 1 0 0 1 1 0 0 1
0 1 0 0 1 1 0 0 0 1 1 0 0 1 0 1 0 0 0 0 0 0 0 0 1 0 0 1 1 0 0
0 0 1 0 0 0 1 1 0 0 0 0 1 0 0 0 0 0 0 0 0 1 0 0 0 0 0 0 0 1 1
0 0 1 1 0 0 0 1 0 1 1 0 1 0 0 0 0 0 0 0 0 0 0 0 0 1 1 0 0 0 1
0 0 1 1 0 0 1 0 0 1 0 0 1 0 1 0 0 0 0 0 0 0 0 0 0 1 1 0 0 1 0
0 1 0 1 1 1 1 1 0 1 1 1 0 1 1 0 0 0 0 0 0 0 0 0 1 0 1 1 1 1 1
0 1 1 1 1 1 0 1 0 1 0 1 1 1 1 0 0 0 0 0 0 0 0 1 0 0 1 1 1 1 1
0 0 0 1 1 0 1 1 0 1 1 1 1 0 1 0 0 0 0 0 0 0 0 0 0 0 1 1 0 1 1
0 1 0 0 0 0 0 0 0 1 1 0 0 1 0 0 0 0 0 0 0 0 0 0 1 0 0 0 0 0 0
0 1 1 0 1 0 1 0 0 0 1 0 1 0 1 1 0 0 0 0 0 0 1 0 0 0 1 0 1 0 0
0 0 0 1 0 1 0 0 0 1 0 1 1 0 1 0 0 0 0 0 0 0 0 0 0 0 1 0 1 0 0
0 0 0 1 0 0 0 0 0 0 0 0 0 1 1 1 0 0 0 0 0 0 1 0 0 0 0 0 0 1 0
0 1 0 1 0 0 1 1 0 1 1 1 0 1 0 0 0 0 0 0 0 0 0 0 1 0 1 0 0 1 1
0 0 0 0 0 0 0 1 0 0 1 0 0 1 0 1 0 0 0 0 0 0 0 0 0 0 0 0 0 0 1
0 0 1 0 1 1 1 1 0 1 0 0 1 1 1 0 0 0 0 0 0 0 0 0 0 1 0 1 1 1 1
0 1 1 0 0 0 0 1 0 0 0 1 0 1 0 0 0 0 0 0 0 1 0 0 0 0 1 0 0 0 1
0 0 0 0 0 0 0 1 0 0 1 0 1 1 1 1 0 0 0 0 0 0 0 0 0 0 0 0 0 0 1
0 1 1 0 0 0 1 0 0 0 0 1 0 0 1 1 0 0 0 0 0 1 0 1 0 0 0 0 0 1 1
0 0 1 0 0 0 1 1 0 1 1 0 1 1 0 1 0 0 0 0 0 0 0 0 0 1 0 0 0 1 1
0 0 0 1 1 0 1 0 0 1 0 0 1 0 0 0 0 0 0 0 0 0 0 0 0 0 1 1 0 1 0
0 1 0 0 1 1 0 0 0 1 0 1 0 1 0 0 0 0 0 0 0 0 0 0 1 0 0 1 1 0 0
0 1 0 0 0 0 1 0 0 0 0 1 0 0 0 0 0 0 0 0 0 1 0 0 0 0 0 0 0 1 0
0 0 0 1 0 1 1 0 0 0 1 1 0 1 0 1 0 0 0 0 0 0 0 0 0 0 1 0 1 1 0
0 1 1 0 0 1 0 0 0 0 1 1 1 0 1 0 0 0 0 0 0 0 0 1 0 1 0 1 0 1 0
0 1 0 0 0 0 0 0 0 0 0 0 1 1 0 1 0 0 0 0 0 1 0 0 0 0 0 1 1 0 0
0 0 1 1 0 1 1 1 0 0 0 1 1 1 1 1 0 0 0 0 0 0 0 1 0 0 1 1 0 0 0
0 0 0 0 1 1 1 0 0 1 0 0 0 1 0 0 0 0 0 0 0 0 0 0 0 0 0 1 1 1 0
0 1 1 0 0 1 0 1 0 0 1 0 0 0 0 1 0 0 0 0 0 0 1 1 0 0 0 0 0 1 0
0 1 0 1 0 0 1 0 0 1 1 1 0 0 1 0 0 0 0 0 0 0 0 0 1 0 1 0 0 1 0
0 0 1 1 1 0 0 0 0 0 0 1 0 0 0 0 0 0 0 0 0 0 1 1 0 0 0 1 0 0 0
0 0 1 0 1 0 0 0 0 0 1 1 1 0 1 0 0 0 0 0 0 0 0 0 0 1 0 1 0 0 0
0 0 0 0 1 0 0 0 0 1 1 1 0 0 0 1 0 0 0 0 0 0 0 0 0 0 0 1 0 0 0
0 0 0 0 0 0 1 0 0 1 0 0 1 1 1 0 0 0 0 0 0 0 0 0 0 0 0 0 0 1 0
0 1 1 0 1 1 0 1 0 0 0 1 0 1 1 1 0 0 0 0 0 1 0 0 0 0 1 0 0 0 1
0 1 0 0 0 0 1 1 0 0 1 1 1 1 0 0 0 0 0 0 0 0 0 1 0 0 0 0 1 1 1
0 1 0 1 0 1 1 0 0 1 0 0 1 1 0 1 0 0 0 0 0 0 0 1 0 0 0 1 0 0 1
0 1 1 1 0 0 0 0 0 1 1 0 0 1 1 0 0 0 0 0 0 0 0 1 0 0 0 1 0 1 0
0 0 0 0 0 1 0 0 0 1 0 0 1 1 1 0 0 0 0 0 0 0 0 0 0 0 0 0 1 0 0
0 0 1 0 0 1 0 1 0 0 1 1 0 1 0 1 0 0 0 0 0 0 0 0 0 1 0 0 1 0 1
0 0 1 1 1 1 0 0 0 0 0 0 1 0 1 1 0 0 0 0 0 1 0 1 0 0 0 0 1 0 1
0 1 0 1 1 1 1 0 0 1 1 0 0 1 1 0 0 0 0 0 0 0 0 0 1 0 1 1 1 1 0
0 0 1 0 1 0 1 0 0 0 1 1 1 0 0 0 0 0 0 0 0 0 0 0 0 1 0 1 0 1 0
0 1 1 0 1 0 0 1 0 0 1 1 1 0 1 0 0 0 0 0 0 0 0 1 0 1 0 1 1 1 1
0 1 0 1 0 0 0 0 0 1 0 0 1 0 0 0 0 0 0 0 0 0 0 1 0 0 0 1 0 0 0
0 1 1 1 0 1 0 0 0 1 0 1 0 1 1 0 0 0 0 0 0 0 0 1 0 0 1 1 1 1 0
0 1 0 0 0 1 1 1 0 1 0 1 0 0 1 0 0 0 0 0 0 0 0 0 1 0 0 0 1 1 1
0 0 0 1 0 0 0 0 0 1 0 0 1 1 0 1 0 0 0 0 0 0 0 0 0 0 1 0 0 0 0
0 1 0 1 0 0 1 1 0 1 0 0 0 1 1 0 0 0 0 0 0 0 0 1 0 0 0 1 1 0 1
0 0 1 0 0 0 0 0 0 1 1 0 1 1 1 0 0 0 0 0 0 0 0 0 0 1 0 0 0 0 0
0 0 0 0 1 1 1 1 0 0 1 0 1 1 1 1 0 0 0 0 0 0 0 0 0 0 0 1 1 1 1
0 0 0 0 0 0 1 1 0 1 0 1 1 0 0 1 0 0 0 0 0 0 0 0 0 0 0 0 0 1 1
0 1 1 0 1 0 0 0 0 0 1 1 0 1 1 1 0 0 0 0 0 0 0 1 0 1 1 0 0 0 1
0 1 0 1 1 0 0 0 0 1 0 0 0 1 0 0 0 0 0 0 0 0 0 1 0 0 1 0 1 0 0
0 0 0 1 0 1 1 1 0 0 1 1 1 0 1 1 0 0 0 0 0 0 0 0 0 0 1 0 1 1 1
0 1 1 1 1 1 1 0 0 1 1 1 1 1 1 0 0 0 0 0 0 0 0 1 0 0 0 0 0 0 0
0 1 1 0 0 0 0 1 0 0 1 0 0 0 1 0 0 0 0 0 0 0 1 0 0 0 1 1 1 0 1
0 0 1 0 0 1 1 0 0 1 1 1 1 1 1 1 0 0 0 0 0 0 0 0 0 1 0 0 1 1 0
0 0 1 0 0 0 1 0 0 1 1 0 1 0 1 0 0 0 0 0 0 0 0 0 0 1 0 0 0 1 0
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*/
