// Digital circuit left_shift.dig as structural Verilog
module left_shift (
  input  C,
  input  Clr,
  input  IN0,
  input  IN1,
  input  IN2,
  input  IN3,
  input  IN4,
  input  IN5,
  input  IN6,
  input  IN7,
  input  Circ,
  output O0,
  output O1,
  output O2,
  output O3,
  output O4,
  output O5,
  output O6,
  output O7
);

  wire and_1_out;

  and and_1 (and_1_out, O7, Circ);
  D_FF_AS d_ff_as_1 (.Set(IN0), .D(and_1_out), .C(C), .Clr(Clr), .Q(O0));  // open: nQ
  D_FF_AS d_ff_as_2 (.Set(IN1), .D(O0), .C(C), .Clr(Clr), .Q(O1));  // open: nQ
  D_FF_AS d_ff_as_3 (.Set(IN2), .D(O1), .C(C), .Clr(Clr), .Q(O2));  // open: nQ
  D_FF_AS d_ff_as_4 (.Set(IN3), .D(O2), .C(C), .Clr(Clr), .Q(O3));  // open: nQ
  D_FF_AS d_ff_as_5 (.Set(IN4), .D(O3), .C(C), .Clr(Clr), .Q(O4));  // open: nQ
  D_FF_AS d_ff_as_6 (.Set(IN5), .D(O4), .C(C), .Clr(Clr), .Q(O5));  // open: nQ
  D_FF_AS d_ff_as_7 (.Set(IN6), .D(O5), .C(C), .Clr(Clr), .Q(O6));  // open: nQ
  D_FF_AS d_ff_as_8 (.Set(IN7), .D(O6), .C(C), .Clr(Clr), .Q(O7));  // open: nQ
endmodule
