// Digital circuit multiplier.dig as structural Verilog
module multiplier (
  input  a0,
  input  a1,
  input  a2,
  input  a3,
  input  a4,
  input  a5,
  input  a6,
  input  b0,
  input  b1,
  input  b2,
  input  b3,
  input  b4,
  input  b5,
  input  b6,
  input  a7,
  input  b7,
  output o0,
  output o1,
  output o2,
  output o3,
  output o4,
  output o5,
  output o6,
  output o7,
  output o8,
  output o9,
  output o10,
  output o11,
  output o12,
  output o13,
  output sgn
);

  wire _8bit_adder_1_o1, _8bit_adder_1_o2, _8bit_adder_1_o3, _8bit_adder_1_o4, _8bit_adder_1_o5,
       _8bit_adder_1_o6, _8bit_adder_1_o7, _8bit_adder_2_o1, _8bit_adder_2_o2, _8bit_adder_2_o3,
       _8bit_adder_2_o4, _8bit_adder_2_o5, _8bit_adder_2_o6, _8bit_adder_2_o7, _8bit_adder_3_o1,
       _8bit_adder_3_o2, _8bit_adder_3_o3, _8bit_adder_3_o4, _8bit_adder_3_o5, _8bit_adder_3_o6,
       _8bit_adder_3_o7, _8bit_adder_4_o1, _8bit_adder_4_o2, _8bit_adder_4_o3, _8bit_adder_4_o4,
       _8bit_adder_4_o5, _8bit_adder_4_o6, _8bit_adder_4_o7, _8bit_adder_5_o1, _8bit_adder_5_o2,
       _8bit_adder_5_o3, _8bit_adder_5_o4, _8bit_adder_5_o5, _8bit_adder_5_o6, _8bit_adder_5_o7, and_2_out,
       and_3_out, and_4_out, and_5_out, and_6_out, and_7_out, and_8_out, and_9_out, and_10_out, and_11_out,
       and_12_out, and_13_out, and_14_out, and_15_out, and_16_out, and_17_out, and_18_out, and_19_out,
       and_20_out, and_21_out, and_22_out, and_23_out, and_24_out, and_25_out, and_26_out, and_27_out,
       and_28_out, and_29_out, and_30_out, and_31_out, and_32_out, and_33_out, and_34_out, and_35_out,
       and_36_out, and_37_out, and_38_out, and_39_out, and_40_out, and_41_out, and_42_out, and_43_out,
       and_44_out, and_45_out, and_46_out, and_47_out, and_48_out, and_49_out;

  and and_1 (o0, a0, b0);
  and and_2 (and_2_out, a1, b0);
  and and_3 (and_3_out, a2, b0);
  and and_4 (and_4_out, a3, b0);
  and and_5 (and_5_out, a4, b0);
  and and_6 (and_6_out, a5, b0);
  and and_7 (and_7_out, a6, b0);
  and and_8 (and_8_out, a0, b1);
  and and_9 (and_9_out, a1, b1);
  and and_10 (and_10_out, a2, b1);
  and and_11 (and_11_out, a3, b1);
  and and_12 (and_12_out, a4, b1);
  and and_13 (and_13_out, a5, b1);
  and and_14 (and_14_out, a6, b1);
  _8bit_adder _8bit_adder_1 (
    .A0(and_2_out), .B0(and_8_out), .A1(and_9_out), .B1(and_3_out), .A2(and_10_out), .B2(and_4_out),
    .A3(and_11_out), .B3(and_5_out), .A4(and_12_out), .B4(and_6_out), .A5(and_13_out), .B5(and_7_out),
    .A6(and_14_out), .B6(1'b0), .A7(1'b0), .B7(1'b0), .C(1'b0), .O0(o1), .O1(_8bit_adder_1_o1),
    .O2(_8bit_adder_1_o2), .O3(_8bit_adder_1_o3), .O4(_8bit_adder_1_o4), .O5(_8bit_adder_1_o5),
    .O6(_8bit_adder_1_o6), .O7(_8bit_adder_1_o7));  // open: Overflow
  and and_15 (and_15_out, a0, b2);
  and and_16 (and_16_out, a1, b2);
  and and_17 (and_17_out, a2, b2);
  and and_18 (and_18_out, a3, b2);
  and and_19 (and_19_out, a4, b2);
  and and_20 (and_20_out, a5, b2);
  and and_21 (and_21_out, a6, b2);
  _8bit_adder _8bit_adder_2 (
    .A0(and_15_out), .B0(_8bit_adder_1_o1), .A1(and_16_out), .B1(_8bit_adder_1_o2), .A2(and_17_out),
    .B2(_8bit_adder_1_o3), .A3(and_18_out), .B3(_8bit_adder_1_o4), .A4(and_19_out), .B4(_8bit_adder_1_o5),
    .A5(and_20_out), .B5(_8bit_adder_1_o6), .A6(and_21_out), .B6(_8bit_adder_1_o7), .A7(1'b0), .B7(1'b0),
    .C(1'b0), .O0(o2), .O1(_8bit_adder_2_o1), .O2(_8bit_adder_2_o2), .O3(_8bit_adder_2_o3),
    .O4(_8bit_adder_2_o4), .O5(_8bit_adder_2_o5), .O6(_8bit_adder_2_o6), .O7(_8bit_adder_2_o7));  // open: Overflow
  and and_22 (and_22_out, a0, b3);
  and and_23 (and_23_out, a1, b3);
  and and_24 (and_24_out, a2, b3);
  and and_25 (and_25_out, a3, b3);
  and and_26 (and_26_out, a4, b3);
  and and_27 (and_27_out, a5, b3);
  and and_28 (and_28_out, a6, b3);
  _8bit_adder _8bit_adder_3 (
    .A0(and_22_out), .B0(_8bit_adder_2_o1), .A1(and_23_out), .B1(_8bit_adder_2_o2), .A2(and_24_out),
    .B2(_8bit_adder_2_o3), .A3(and_25_out), .B3(_8bit_adder_2_o4), .A4(and_26_out), .B4(_8bit_adder_2_o5),
    .A5(and_27_out), .B5(_8bit_adder_2_o6), .A6(and_28_out), .B6(_8bit_adder_2_o7), .A7(1'b0), .B7(1'b0),
    .C(1'b0), .O0(o3), .O1(_8bit_adder_3_o1), .O2(_8bit_adder_3_o2), .O3(_8bit_adder_3_o3),
    .O4(_8bit_adder_3_o4), .O5(_8bit_adder_3_o5), .O6(_8bit_adder_3_o6), .O7(_8bit_adder_3_o7));  // open: Overflow
  and and_29 (and_29_out, a0, b4);
  and and_30 (and_30_out, a1, b4);
  and and_31 (and_31_out, a2, b4);
  and and_32 (and_32_out, a3, b4);
  and and_33 (and_33_out, a4, b4);
  and and_34 (and_34_out, a5, b4);
  and and_35 (and_35_out, a6, b4);
  _8bit_adder _8bit_adder_4 (
    .A0(and_29_out), .B0(_8bit_adder_3_o1), .A1(and_30_out), .B1(_8bit_adder_3_o2), .A2(and_31_out),
    .B2(_8bit_adder_3_o3), .A3(and_32_out), .B3(_8bit_adder_3_o4), .A4(and_33_out), .B4(_8bit_adder_3_o5),
    .A5(and_34_out), .B5(_8bit_adder_3_o6), .A6(and_35_out), .B6(_8bit_adder_3_o7), .A7(1'b0), .B7(1'b0),
    .C(1'b0), .O0(o4), .O1(_8bit_adder_4_o1), .O2(_8bit_adder_4_o2), .O3(_8bit_adder_4_o3),
    .O4(_8bit_adder_4_o4), .O5(_8bit_adder_4_o5), .O6(_8bit_adder_4_o6), .O7(_8bit_adder_4_o7));  // open: Overflow
  and and_36 (and_36_out, a0, b5);
  and and_37 (and_37_out, a1, b5);
  and and_38 (and_38_out, a2, b5);
  and and_39 (and_39_out, a3, b5);
  and and_40 (and_40_out, a4, b5);
  and and_41 (and_41_out, a5, b5);
  and and_42 (and_42_out, a6, b5);
  _8bit_adder _8bit_adder_5 (
    .A0(and_36_out), .B0(_8bit_adder_4_o1), .A1(and_37_out), .B1(_8bit_adder_4_o2), .A2(and_38_out),
    .B2(_8bit_adder_4_o3), .A3(and_39_out), .B3(_8bit_adder_4_o4), .A4(and_40_out), .B4(_8bit_adder_4_o5),
    .A5(and_41_out), .B5(_8bit_adder_4_o6), .A6(and_42_out), .B6(_8bit_adder_4_o7), .A7(1'b0), .B7(1'b0),
    .C(1'b0), .O0(o5), .O1(_8bit_adder_5_o1), .O2(_8bit_adder_5_o2), .O3(_8bit_adder_5_o3),
    .O4(_8bit_adder_5_o4), .O5(_8bit_adder_5_o5), .O6(_8bit_adder_5_o6), .O7(_8bit_adder_5_o7));  // open: Overflow
  and and_43 (and_43_out, a0, b6);
  and and_44 (and_44_out, a1, b6);
  and and_45 (and_45_out, a2, b6);
  and and_46 (and_46_out, a3, b6);
  and and_47 (and_47_out, a4, b6);
  and and_48 (and_48_out, a5, b6);
  and and_49 (and_49_out, a6, b6);
  _8bit_adder _8bit_adder_6 (
    .A0(and_43_out), .B0(_8bit_adder_5_o1), .A1(and_44_out), .B1(_8bit_adder_5_o2), .A2(and_45_out),
    .B2(_8bit_adder_5_o3), .A3(and_46_out), .B3(_8bit_adder_5_o4), .A4(and_47_out), .B4(_8bit_adder_5_o5),
    .A5(and_48_out), .B5(_8bit_adder_5_o6), .A6(and_49_out), .B6(_8bit_adder_5_o7), .A7(1'b0), .B7(1'b0),
    .C(1'b0), .O0(o6), .O1(o7), .O2(o8), .O3(o9), .O4(o10), .O5(o11), .O6(o12), .O7(o13));  // open: Overflow
  xor xor_1 (sgn, a7, b7);
endmodule

/* Test case:
a7 a6 a5 a4 a3 a2 a1 a0 b7 b6 b5 b4 b3 b2 b1 b0 sgn o13 o12 o11 o10 o9 o8 o7 o6 o5 o4 o3 o2 o1 o0
0 1 0 1 0 1 1 1 0 1 0 0 1 1 1 1 0 0 1 1 0 1 0 1 1 0 1 1 0 0 1
1 0 1 1 1 1 1 0 0 1 0 0 0 1 0 1 1 0 1 0 0 0 0 1 0 1 1 0 1 1 0
0 0 1 1 1 1 1 0 0 1 1 1 0 0 0 0 0 0 1 1 0 1 1 0 0 1 0 0 0 0 0
0 0 1 0 0 1 0 1 0 0 1 0 0 1 0 0 0 0 0 0 1 0 1 0 0 1 1 0 1 0 0
0 0 0 1 0 0 0 1 0 1 0 0 1 1 1 0 0 0 0 0 1 0 1 0 0 1 0 1 1 1 0
1 1 0 0 1 0 1 0 1 0 0 1 0 1 1 1 0 0 0 0 1 1 0 1 0 1 0 0 1 1 0
1 1 0 1 0 0 0 0 0 1 1 1 0 1 0 1 1 1 0 0 1 0 0 1 0 0 1 0 0 0 0
1 1 1 1 0 0 1 0 1 0 1 1 1 0 0 0 0 0 1 1 0 0 0 1 1 1 1 0 0 0 0
1 0 1 0 1 1 0 0 1 1 0 1 0 0 0 1 0 0 0 1 1 0 1 1 1 1 0 1 1 0 0
0 0 0 0 1 0 0 1 1 0 1 0 1 0 0 0 1 0 0 0 0 0 1 0 1 1 0 1 0 0 0
1 0 1 1 0 0 1 1 0 1 1 1 1 0 1 1 1 0 1 1 0 0 0 1 0 0 0 0 0 0 1
0 1 1 1 0 0 1 0 0 0 1 1 0 0 0 0 0 0 1 0 1 0 1 0 1 1 0 0 0 0 0
1 1 0 1 0 0 0 1 1 0 0 0 0 1 0 1 0 0 0 0 0 0 1 1 0 0 1 0 1 0 1
1 0 0 1 1 0 1 0 1 0 1 0 0 0 1 1 0 0 0 0 0 1 1 1 0 0 0 1 1 1 0
1 1 1 0 1 0 0 1 1 0 1 1 1 0 0 0 0 0 1 0 1 1 0 1 1 1 1 1 0 0 0
0 0 1 1 0 0 1 1 0 0 1 0 1 1 1 0 0 0 0 1 0 0 1 0 0 1 0 1 0 1 0
1 1 0 0 0 0 1 0 0 0 1 0 1 0 1 0 1 0 0 1 0 1 0 1 1 0 1 0 1 0 0
0 0 1 0 1 0 0 0 1 0 1 0 1 0 1 0 1 0 0 0 1 1 0 1 0 0 1 0 0 0 0
1 1 1 0 0 0 1 0 1 1 1 1 0 1 1 0 0 1 0 1 1 0 1 0 0 1 0 1 1 0 0
0 0 0 1 1 0 0 1 0 1 0 1 0 1 0 0 0 0 0 1 0 0 0 0 0 1 1 0 1 0 0
1 1 1 0 0 0 0 0 0 1 0 0 1 0 0 1 1 0 1 1 0 1 1 0 1 1 0 0 0 0 0
0 1 0 0 1 0 1 1 1 1 1 0 0 0 1 0 1 0 1 1 1 0 0 1 0 1 1 0 1 1 0
1 0 0 0 0 1 1 0 0 0 1 0 0 1 0 0 1 0 0 0 0 0 0 1 1 0 1 1 0 0 0
1 0 1 1 1 0 1 1 1 1 0 0 1 1 1 1 0 0 1 0 0 1 0 0 0 1 1 0 1 0 1
1 1 1 1 1 0 1 0 1 0 0 0 1 0 1 0 0 0 0 0 1 0 0 1 1 0 0 0 1 0 0
1 0 1 1 0 0 0 1 1 0 1 1 0 1 1 1 0 0 0 1 0 1 0 1 0 0 0 0 1 1 1
0 1 1 1 0 0 1 1 1 0 1 0 0 1 0 0 1 0 1 0 0 0 0 0 0 1 0 1 1 0 0
1 1 0 0 1 0 1 0 1 0 1 1 1 1 0 1 0 0 1 0 0 0 1 1 0 1 0 0 0 1 0
1 1 0 1 1 0 1 1 0 1 1 1 0 1 0 0 1 1 0 1 0 0 1 0 0 1 1 1 1 0 0
1 1 0 0 0 1 1 1 1 0 0 1 1 1 0 1 0 0 0 1 0 0 0 0 0 0 0 1 0 1 1
0 0 1 1 0 1 0 0 1 0 1 0 0 0 1 1 1 0 0 0 1 1 1 0 0 0 1 1 1 0 0
0 0 1 1 1 1 0 1 0 1 0 0 0 1 0 0 0 0 1 0 0 0 0 0 0 1 1 0 1 0 0
0 0 0 1 0 0 1 1 1 1 0 1 1 0 1 0 1 0 0 0 1 1 0 1 0 1 0 1 1 1 0
1 0 0 1 1 1 1 0 0 0 0 0 0 0 1 0 1 0 0 0 0 0 0 0 0 1 1 1 1 0 0
1 0 1 1 1 1 0 1 0 1 0 0 0 1 1 1 1 0 1 0 0 0 0 1 1 1 0 1 0 1 1
1 1 0 1 0 1 1 1 0 1 0 1 1 1 1 1 1 1 0 0 0 0 0 0 1 0 0 1 0 0 1
0 0 1 0 0 0 1 1 0 0 1 0 1 0 1 0 0 0 0 0 1 0 1 1 0 1 1 1 1 1 0
0 0 0 1 0 1 0 0 0 0 1 1 0 1 0 1 0 0 0 0 1 0 0 0 0 1 0 0 1 0 0
0 1 1 0 1 0 0 0 0 1 1 1 0 0 0 0 0 1 0 1 1 0 1 1 0 0 0 0 0 0 0
1 1 1 1 1 1 0 0 1 1 0 0 0 0 1 0 0 0 1 1 1 1 1 1 1 1 1 1 0 0 0
1 1 1 1 0 1 1 0 1 1 0 1 1 0 0 0 0 1 0 1 0 0 0 1 0 0 1 0 0 0 0
0 1 1 0 0 0 1 0 1 0 0 1 0 0 0 1 1 0 0 0 1 1 0 1 0 0 0 0 0 1 0
0 1 0 1 1 0 1 0 1 0 1 1 0 1 0 1 1 0 1 0 0 1 0 1 0 1 0 0 0 1 0
1 1 0 1 1 0 1 1 0 1 0 1 0 0 1 1 1 0 1 1 1 0 1 1 0 0 0 0 0 0 1
0 1 1 1 1 0 1 1 1 0 0 1 0 0 0 0 1 0 0 0 1 1 1 1 0 1 1 0 0 0 0
1 0 1 1 0 1 0 0 1 1 0 1 1 1 1 0 0 0 1 0 0 1 1 0 0 0 1 1 0 0 0
1 1 1 1 1 1 0 0 0 0 1 1 1 0 1 0 1 0 1 1 1 0 0 0 0 0 1 1 0 0 0
0 0 1 0 0 0 1 1 0 0 0 0 0 1 1 1 0 0 0 0 0 0 0 1 1 1 1 0 1 0 1
0 0 0 1 0 1 0 1 1 1 1 1 1 1 1 0 1 0 0 1 0 1 0 0 1 0 1 0 1 1 0
0 1 1 0 1 1 1 1 0 0 0 1 1 1 1 0 0 0 0 1 1 0 1 0 0 0 0 0 0 1 0
1 1 0 0 0 1 0 0 1 1 0 1 1 0 0 1 0 0 1 0 1 1 1 1 0 1 0 0 1 0 0
0 0 0 0 1 0 0 0 0 0 0 0 0 0 1 0 0 0 0 0 0 0 0 0 0 0 1 0 0 0 0
0 0 1 0 1 1 0 1 0 0 0 0 0 1 0 0 0 0 0 0 0 0 0 1 0 1 1 0 1 0 0
0 0 0 0 1 0 0 0 1 1 1 1 0 1 0 1 1 0 0 0 0 1 1 1 0 1 0 1 0 0 0
0 0 0 0 0 1 0 1 1 1 1 0 1 0 0 1 1 0 0 0 0 1 0 0 0 0 0 1 1 0 1
0 1 0 1 0 1 0 1 0 0 0 1 1 0 0 1 0 0 0 1 0 0 0 0 1 0 0 1 1 0 1
0 1 0 0 1 1 0 0 0 0 0 0 0 0 0 1 0 0 0 0 0 0 0 0 1 0 0 1 1 0 0
1 1 0 0 0 1 0 1 1 0 1 0 1 1 0 1 0 0 0 1 1 0 0 0 0 1 0 0 0 0 1
1 0 1 1 0 1 0 1 1 1 0 1 1 0 0 0 0 0 1 0 0 1 0 0 0 1 1 1 0 0 0
1 0 0 0 0 1 0 0 0 1 1 0 1 1 1 1 1 0 0 0 0 0 1 1 0 1 1 1 1 0 0
0 0 0 1 0 1 0 0 0 0 1 1 1 0 0 0 0 0 0 0 1 0 0 0 1 1 0 0 0 0 0
0 0 1 0 1 0 1 1 0 0 0 1 0 0 1 1 0 0 0 0 0 1 1 0 0 1 1 0 0 0 1
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*/
