// Digital circuit signed_8bit_adder.dig as structural Verilog
module signed_8bit_adder (
  input  A0,
  input  B0,
  input  A1,
  input  B1,
  input  A2,
  input  B2,
  input  A3,
  input  B3,
  input  A4,
  input  B4,
  input  A5,
  input  B5,
  input  A6,
  input  B6,
  input  A7,
  input  B7,
  output o0,
  output o1,
  output o2,
  output o3,
  output o4,
  output o5,
  output o6,
  output o7,
  output sgn
);

  wire _8bit_adder_1_o7, _8bit_adder_2_o0, _8bit_adder_2_o1, _8bit_adder_2_o2, _8bit_adder_2_o3,
       _8bit_adder_2_o4, _8bit_adder_2_o5, _8bit_adder_2_o6, _8bit_comparator_1_a_eq_b,
       _8bit_comparator_1_a_gt_b, and_2_out, and_3_out, and_4_out, not_1_out, not_2_out, or_1_out,
       two_complement_1_o0, two_complement_1_o1, two_complement_1_o2, two_complement_1_o3,
       two_complement_1_o4, two_complement_1_o5, two_complement_1_o6, two_complement_1_sgn,
       two_complement_2_o0, two_complement_2_o1, two_complement_2_o2, two_complement_2_o3,
       two_complement_2_o4, two_complement_2_o5, two_complement_2_o6, two_complement_2_sgn, xnor_1_out;

  xnor xnor_1 (xnor_1_out, A7, B7);
  and and_1 (o7, _8bit_adder_1_o7, xnor_1_out);
  _8bit_adder _8bit_adder_1 (
    .A0(A0), .B0(B0), .A1(A1), .B1(B1), .A2(A2), .B2(B2), .A3(A3), .B3(B3), .A4(A4), .B4(B4), .A5(A5),
    .B5(B5), .A6(A6), .B6(B6), .A7(1'b0), .B7(1'b0), .C(1'b0), .O7(_8bit_adder_1_o7));  // open: O0, O1, O2, O3, O4, O5, O6, Overflow
  _8bit_comparator _8bit_comparator_1 (
    .B7(1'b0), .A7(1'b0), .B6(B6), .A6(A6), .B5(B5), .A5(A5), .B4(B4), .A4(A4), .B3(B3), .A3(A3), .B2(B2),
    .A2(A2), .B1(B1), .A1(A1), .B0(B0), .A0(A0), .A_gt_B(_8bit_comparator_1_a_gt_b),
    .A_eq_B(_8bit_comparator_1_a_eq_b));  // open: A_lt_B
  two_complement two_complement_1 (
    .A8(B7), .A6(B6), .A5(B5), .A4(B4), .A3(B3), .A2(B2), .A1(B1), .A0(B0), .A7(1'b0),
    .O0(two_complement_1_o0), .O1(two_complement_1_o1), .O2(two_complement_1_o2), .O3(two_complement_1_o3),
    .O4(two_complement_1_o4), .O5(two_complement_1_o5), .O6(two_complement_1_o6), .sgn(two_complement_1_sgn));  // open: O7
  two_complement two_complement_2 (
    .A8(A7), .A6(A6), .A5(A5), .A4(A4), .A3(A3), .A2(A2), .A1(A1), .A0(A0), .A7(1'b0),
    .O0(two_complement_2_o0), .O1(two_complement_2_o1), .O2(two_complement_2_o2), .O3(two_complement_2_o3),
    .O4(two_complement_2_o4), .O5(two_complement_2_o5), .O6(two_complement_2_o6), .sgn(two_complement_2_sgn));  // open: O7
  not not_1 (not_1_out, _8bit_comparator_1_a_gt_b);
  not not_2 (not_2_out, _8bit_comparator_1_a_eq_b);
  and and_2 (and_2_out, A7, _8bit_comparator_1_a_gt_b);
  and and_3 (and_3_out, A7, B7);
  and and_4 (and_4_out, not_2_out, not_1_out, B7);
  or or_1 (or_1_out, and_2_out, and_3_out, and_4_out);
  _8bit_adder _8bit_adder_2 (
    .A0(two_complement_2_o0), .B0(two_complement_1_o0), .A1(two_complement_2_o1), .B1(two_complement_1_o1),
    .A2(two_complement_2_o2), .B2(two_complement_1_o2), .A3(two_complement_2_o3), .B3(two_complement_1_o3),
    .A4(two_complement_2_o4), .B4(two_complement_1_o4), .A5(two_complement_2_o5), .B5(two_complement_1_o5),
    .A6(two_complement_2_o6), .B6(two_complement_1_o6), .A7(two_complement_2_sgn), .B7(two_complement_1_sgn),
    .C(1'b0), .O0(_8bit_adder_2_o0), .O1(_8bit_adder_2_o1), .O2(_8bit_adder_2_o2), .O3(_8bit_adder_2_o3),
    .O4(_8bit_adder_2_o4), .O5(_8bit_adder_2_o5), .O6(_8bit_adder_2_o6));  // open: O7, Overflow
  two_complement two_complement_3 (
    .A8(or_1_out), .A6(_8bit_adder_2_o6), .A5(_8bit_adder_2_o5), .A4(_8bit_adder_2_o4),
    .A3(_8bit_adder_2_o3), .A2(_8bit_adder_2_o2), .A1(_8bit_adder_2_o1), .A0(_8bit_adder_2_o0), .A7(1'b0),
    .O0(o0), .O1(o1), .O2(o2), .O3(o3), .O4(o4), .O5(o5), .O6(o6), .sgn(sgn));  // open: O7
endmodule

/* Test case:
A7 A6 A5 A4 A3 A2 A1 A0 B7 B6 B5 B4 B3 B2 B1 B0 sgn o7 o6 o5 o4 o3 o2 o1 o0
1 0 0 0 0 0 0 1 0 1 1 0 1 1 0 1 0 0 1 1 0 1 1 0 0
1 0 1 0 1 0 0 1 0 1 0 1 0 1 0 0 0 0 0 1 0 1 0 1 1
0 1 0 0 0 1 0 0 0 0 1 1 1 0 0 0 0 0 1 1 1 1 1 0 0
0 1 1 1 0 1 1 1 0 0 0 1 0 1 1 0 0 1 0 0 0 1 1 0 1
1 1 1 0 0 0 1 0 1 0 1 0 1 0 0 1 1 1 0 0 0 1 0 1 1
1 1 1 0 0 0 1 1 1 1 1 1 1 1 1 1 1 1 1 1 0 0 0 1 0
1 1 0 1 1 0 0 0 0 1 1 1 1 1 1 0 0 0 0 1 0 0 1 1 0
0 1 1 0 1 1 1 0 0 0 0 0 0 1 1 1 0 0 1 1 1 0 1 0 1
0 1 0 1 0 1 1 1 1 1 1 0 0 0 0 1 1 0 0 0 0 1 0 1 0
1 1 0 0 1 1 0 0 0 0 1 1 0 0 0 1 1 0 0 0 1 1 0 1 1
0 0 1 0 0 1 0 0 0 1 0 0 0 0 0 0 0 0 1 1 0 0 1 0 0
1 0 1 1 1 1 0 0 0 0 0 1 0 1 0 0 1 0 0 1 0 1 0 0 0
1 0 1 1 1 0 1 0 0 1 1 0 0 1 1 0 0 0 0 1 0 1 1 0 0
1 1 1 1 1 0 1 1 0 0 1 0 0 1 1 0 1 0 1 0 1 0 1 0 1
1 0 0 1 1 0 1 1 1 0 1 0 0 0 0 0 1 0 0 1 1 1 0 1 1
0 1 0 1 0 0 1 0 0 0 1 1 0 1 0 0 0 1 0 0 0 0 1 1 0
0 0 0 1 1 0 0 0 0 0 1 1 0 1 0 1 0 0 1 0 0 1 1 0 1
1 1 1 1 1 1 0 1 1 1 1 1 0 1 0 1 1 1 1 1 1 0 0 1 0
1 0 1 1 0 1 1 1 1 0 0 0 0 1 0 1 1 0 0 1 1 1 1 0 0
0 0 1 1 1 0 1 0 0 0 1 1 0 0 1 0 0 0 1 1 0 1 1 0 0
0 0 1 0 0 0 0 0 0 1 1 0 0 0 1 0 0 1 0 0 0 0 0 1 0
1 0 0 1 1 1 0 1 1 0 1 0 1 1 1 1 1 0 1 0 0 1 1 0 0
1 0 0 1 1 0 1 1 1 1 1 1 0 1 1 1 1 1 0 0 1 0 0 1 0
1 0 0 0 1 1 1 1 0 0 1 1 1 0 0 0 0 0 0 1 0 1 0 0 1
1 0 1 1 1 1 1 0 1 0 0 1 0 1 0 1 1 0 1 0 1 0 0 1 1
1 1 1 1 0 1 1 0 0 1 1 1 1 0 1 0 0 0 0 0 0 0 1 0 0
0 1 0 0 1 1 1 1 0 0 1 1 1 1 1 1 0 1 0 0 0 1 1 1 0
1 1 1 0 0 1 0 0 0 0 0 1 0 1 1 1 1 0 1 0 0 1 1 0 1
0 1 0 1 0 1 0 0 1 0 0 1 1 1 0 0 0 0 0 1 1 1 0 0 0
1 1 0 1 0 1 0 0 1 1 1 0 0 1 0 1 1 1 0 1 1 1 0 0 1
1 1 0 0 1 1 1 0 0 0 0 0 0 1 1 1 1 0 1 0 0 0 1 1 1
0 0 1 1 1 0 1 1 1 1 1 1 1 1 0 1 1 0 1 0 0 0 0 1 0
0 1 1 0 1 0 1 0 0 1 0 0 1 1 0 0 0 1 0 1 1 0 1 1 0
0 1 1 1 1 1 1 1 0 0 1 1 1 0 0 1 0 1 0 1 1 1 0 0 0
0 1 0 0 1 0 0 0 0 0 1 0 0 1 1 1 0 0 1 1 0 1 1 1 1
0 1 0 0 1 0 1 1 1 1 1 1 1 0 0 0 1 0 0 1 0 1 1 0 1
1 1 1 0 0 1 0 1 1 0 0 0 0 0 1 1 1 0 1 1 0 1 0 0 0
1 0 1 0 0 1 0 1 0 1 1 1 1 1 1 1 0 0 1 0 1 1 0 1 0
0 1 0 0 1 0 0 1 0 1 1 1 1 0 1 1 0 1 1 0 0 0 1 0 0
1 1 0 1 0 0 0 1 0 0 1 0 1 1 0 0 1 0 0 1 0 0 1 0 1
1 0 0 0 0 0 1 0 0 0 1 1 0 0 0 1 0 0 0 1 0 1 1 1 1
0 0 0 0 0 0 0 1 1 1 1 1 0 1 1 0 1 0 1 1 1 0 1 0 1
0 1 1 0 0 1 0 1 1 0 1 1 1 0 1 1 0 0 0 1 0 1 0 1 0
1 1 1 1 1 1 0 0 0 0 0 1 1 1 1 1 1 0 1 0 1 1 1 0 1
1 0 0 1 0 1 0 0 0 0 1 1 0 1 1 1 0 0 0 1 0 0 0 1 1
0 0 1 0 1 1 1 1 0 0 1 0 1 1 1 1 0 0 1 0 1 1 1 1 0
1 0 1 0 1 0 0 0 1 1 0 0 0 1 1 1 1 0 1 1 0 1 1 1 1
0 1 0 0 1 0 0 0 0 0 1 1 0 0 1 0 0 0 1 1 1 1 0 1 0
0 1 1 0 1 1 0 1 1 1 1 1 0 1 0 1 1 0 0 0 0 1 0 0 0
1 1 0 1 1 1 0 0 1 1 0 1 0 1 1 0 1 1 0 1 1 0 0 1 0
0 0 0 0 1 0 0 0 1 0 0 1 0 1 0 0 1 0 0 0 0 1 1 0 0
1 0 0 0 0 1 0 0 0 0 1 0 1 0 1 0 0 0 0 1 0 0 1 1 0
1 0 0 0 0 0 0 1 1 0 0 0 1 1 1 1 1 0 0 0 1 0 0 0 0
0 0 1 0 0 0 1 0 0 0 0 1 0 1 1 0 0 0 0 1 1 1 0 0 0
1 1 1 0 0 0 1 0 0 0 1 1 0 1 0 0 1 0 0 1 0 1 1 1 0
0 0 0 1 0 1 0 1 0 1 0 1 1 1 1 0 0 0 1 1 1 0 0 1 1
0 1 1 0 1 0 0 1 1 0 0 1 0 0 0 1 0 0 1 0 1 1 0 0 0
0 1 1 0 1 1 0 0 1 1 0 1 0 0 1 1 0 0 0 0 1 1 0 0 1
0 1 0 0 1 0 1 1 0 1 1 1 0 0 1 0 0 1 0 1 1 1 1 0 1
0 0 1 0 0 1 1 0 0 0 0 1 0 0 1 0 0 0 0 1 1 1 0 0 0
1 1 0 0 1 1 1 1 1 0 1 0 0 1 1 1 1 0 1 1 1 0 1 1 0
1 0 0 1 0 1 0 0 0 1 0 0 0 1 1 0 0 0 0 1 1 0 0 1 0
1 1 1 0 1 0 0 1 1 1 1 0 1 1 0 1 1 1 1 0 1 0 1 1 0
0 0 1 1 1 1 0 1 0 0 0 1 1 0 0 0 0 0 1 0 1 0 1 0 1
0 1 0 0 1 0 1 0 1 0 0 0 1 0 0 1 0 0 1 0 0 0 0 0 1
0 1 0 1 1 0 0 0 0 1 1 1 0 1 1 1 0 1 1 0 0 1 1 1 1
1 1 1 0 1 0 0 1 0 0 0 0 1 1 1 1 1 0 1 0 1 1 0 1 0
1 1 1 0 1 1 1 0 1 1 0 1 0 1 0 1 1 1 1 0 0 0 0 1 1
1 0 1 1 1 1 1 0 0 0 0 0 0 1 0 0 1 0 0 1 1 1 0 1 0
0 0 0 1 1 0 0 0 0 1 0 0 0 1 1 0 0 0 1 0 1 1 1 1 0
1 0 1 0 1 0 1 1 1 1 1 1 1 1 1 1 1 1 0 1 0 1 0 1 0
0 1 1 0 1 1 1 0 0 1 0 0 1 0 1 0 0 1 0 1 1 1 0 0 0
0 0 1 0 1 0 1 1 1 1 1 1 1 0 1 0 1 0 1 0 0 1 1 1 1
1 0 1 0 0 1 0 1 0 0 0 1 0 1 1 0 1 0 0 0 0 1 1 1 1
1 0 0 1 0 0 0 1 1 0 0 0 0 0 1 0 1 0 0 0 1 0 0 1 1
1 0 0 1 1 1 1 1 1 1 1 1 1 1 0 0 1 1 0 0 1 1 0 1 1
0 1 1 1 1 1 1 1 0 0 0 1 1 0 0 1 0 1 0 0 1 1 0 0 0
0 1 1 0 0 1 0 0 1 0 1 0 1 0 0 1 0 0 0 1 1 1 0 1 1
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*/
