// Digital circuit two_complement.dig as structural Verilog
module two_complement (
  input  A8,
  input  A6,
  input  A5,
  input  A4,
  input  A3,
  input  A2,
  input  A1,
  input  A0,
  input  A7,
  output O0,
  output O1,
  output O2,
  output O3,
  output O4,
  output O5,
  output O6,
  output sgn,
  output O7
);

  wire and_1_out, and_2_out, and_3_out, and_4_out, and_5_out, and_6_out, nand_1_out, nand_2_out, nand_3_out,
       nand_4_out, nand_5_out, nand_6_out, nand_7_out, nand_8_out, nand_9_out, nand_10_out, nand_11_out,
       nand_12_out, nand_13_out, nand_14_out, nand_15_out, nand_16_out, not_1_out, not_2_out, not_3_out,
       not_4_out, not_5_out, not_6_out, not_7_out, not_8_out, not_9_out, not_10_out, xor_1_out, xor_2_out,
       xor_3_out, xor_4_out, xor_5_out, xor_6_out, xor_7_out;

  not not_1 (not_1_out, A8);
  not not_2 (not_2_out, A7);
  not not_3 (not_3_out, A6);
  not not_4 (not_4_out, A5);
  not not_5 (not_5_out, A4);
  not not_6 (not_6_out, A3);
  not not_7 (not_7_out, A2);
  not not_8 (not_8_out, A1);
  not not_9 (not_9_out, A0);
  xor xor_1 (xor_1_out, not_8_out, not_9_out);
  and and_1 (and_1_out, not_8_out, not_9_out);
  xor xor_2 (xor_2_out, not_7_out, and_1_out);
  and and_2 (and_2_out, not_7_out, and_1_out);
  xor xor_3 (xor_3_out, not_6_out, and_2_out);
  and and_3 (and_3_out, not_6_out, and_2_out);
  xor xor_4 (xor_4_out, not_5_out, and_3_out);
  and and_4 (and_4_out, not_5_out, and_3_out);
  xor xor_5 (xor_5_out, not_4_out, and_4_out);
  and and_5 (and_5_out, not_4_out, and_4_out);
  xor xor_6 (xor_6_out, not_3_out, and_5_out);
  and and_6 (and_6_out, not_3_out, and_5_out);
  xor xor_7 (xor_7_out, not_2_out, and_6_out);
  not not_10 (not_10_out, not_9_out);
  nand nand_1 (nand_1_out, A7, not_1_out);
  nand nand_2 (nand_2_out, xor_7_out, A8);
  nand nand_3 (nand_3_out, A6, not_1_out);
  nand nand_4 (nand_4_out, xor_6_out, A8);
  nand nand_5 (nand_5_out, A5, not_1_out);
  nand nand_6 (nand_6_out, xor_5_out, A8);
  nand nand_7 (nand_7_out, A4, not_1_out);
  nand nand_8 (nand_8_out, xor_4_out, A8);
  nand nand_9 (nand_9_out, A3, not_1_out);
  nand nand_10 (nand_10_out, xor_3_out, A8);
  nand nand_11 (nand_11_out, A2, not_1_out);
  nand nand_12 (nand_12_out, xor_2_out, A8);
  nand nand_13 (nand_13_out, A1, not_1_out);
  nand nand_14 (nand_14_out, xor_1_out, A8);
  nand nand_15 (nand_15_out, A0, not_1_out);
  nand nand_16 (nand_16_out, not_10_out, A8);
  nand nand_17 (O7, nand_1_out, nand_2_out);
  nand nand_18 (O6, nand_3_out, nand_4_out);
  nand nand_19 (O5, nand_5_out, nand_6_out);
  nand nand_20 (O4, nand_7_out, nand_8_out);
  nand nand_21 (O3, nand_9_out, nand_10_out);
  nand nand_22 (O2, nand_11_out, nand_12_out);
  nand nand_23 (O1, nand_13_out, nand_14_out);
  nand nand_24 (O0, nand_15_out, nand_16_out);

  assign sgn = A8;
endmodule

/* Test case:
A8 A7 A6 A5 A4 A3 A2 A1 A0 sgn O7 O6 O5 O4 O3 O2 O1 O0
0 1 0 1 0 0 1 1 1 0 1 0 1 0 0 1 1 1
0 0 0 0 1 1 0 0 0 0 0 0 0 1 1 0 0 0
1 1 0 1 0 1 0 0 1 1 0 1 0 1 0 1 1 1
1 0 0 0 0 0 0 1 0 1 1 1 1 1 1 1 1 0
0 0 0 1 0 1 0 0 1 0 0 0 1 0 1 0 0 1
0 0 1 0 0 1 0 0 1 0 0 1 0 0 1 0 0 1
1 1 0 0 1 0 1 1 0 1 0 1 1 0 1 0 1 0
1 1 1 0 1 0 1 0 1 1 0 0 1 0 1 0 1 1
0 0 1 0 0 0 1 1 0 0 0 1 0 0 0 1 1 0
1 0 1 0 0 0 1 1 0 1 1 0 1 1 1 0 1 0
1 1 0 0 1 0 1 0 1 1 0 1 1 0 1 0 1 1
0 0 1 0 1 1 0 0 1 0 0 1 0 1 1 0 0 1
0 0 0 0 0 1 0 1 1 0 0 0 0 0 1 0 1 1
0 0 1 1 1 0 0 1 1 0 0 1 1 1 0 0 1 1
0 1 0 1 1 1 1 0 0 0 1 0 1 1 1 1 0 0
1 0 0 1 1 1 0 0 1 1 1 1 0 0 0 1 1 1
1 0 1 1 0 1 0 0 1 1 1 0 0 1 0 1 1 1
1 0 0 0 1 0 0 0 0 1 1 1 1 1 0 0 0 0
0 1 1 0 1 0 1 0 1 0 1 1 0 1 0 1 0 1
0 0 0 1 0 1 0 0 0 0 0 0 1 0 1 0 0 0
1 1 0 1 0 1 1 0 1 1 0 1 0 1 0 0 1 1
1 0 0 1 1 0 1 1 1 1 1 1 0 0 1 0 0 1
0 0 0 0 1 1 1 1 1 0 0 0 0 1 1 1 1 1
1 0 0 1 0 1 1 0 1 1 1 1 0 1 0 0 1 1
0 0 0 1 0 0 0 0 1 0 0 0 1 0 0 0 0 1
0 1 1 1 0 1 0 0 1 0 1 1 1 0 1 0 0 1
0 0 0 1 0 1 0 1 0 0 0 0 1 0 1 0 1 0
1 1 1 1 1 0 0 1 0 1 0 0 0 0 1 1 1 0
0 1 0 1 0 1 1 0 1 0 1 0 1 0 1 1 0 1
0 0 0 0 0 0 0 0 0 0 0 0 0 0 0 0 0 0
0 0 1 0 1 0 0 0 1 0 0 1 0 1 0 0 0 1
1 0 0 0 0 0 0 0 0 1 0 0 0 0 0 0 0 0
1 1 1 0 0 0 0 1 0 1 0 0 1 1 1 1 1 0
0 0 0 1 0 1 0 1 1 0 0 0 1 0 1 0 1 1
1 0 0 0 0 1 0 1 0 1 1 1 1 1 0 1 1 0
1 1 1 1 0 1 0 1 1 1 0 0 0 1 0 1 0 1
1 1 1 0 0 1 0 0 0 1 0 0 1 1 1 0 0 0
0 0 1 1 0 1 1 1 1 0 0 1 1 0 1 1 1 1
0 0 0 1 0 1 1 1 0 0 0 0 1 0 1 1 1 0
1 0 0 1 1 1 1 0 0 1 1 1 0 0 0 1 0 0
0 0 1 0 1 0 1 0 0 0 0 1 0 1 0 1 0 0
1 0 1 1 1 0 0 0 1 1 1 0 0 0 1 1 1 1
1 1 1 0 0 0 1 0 1 1 0 0 1 1 1 0 1 1
1 0 0 1 0 1 1 0 1 1 1 1 0 1 0 0 1 1
0 1 1 1 0 0 0 1 0 0 1 1 1 0 0 0 1 0
1 0 0 0 1 1 0 0 0 1 1 1 1 0 1 0 0 0
1 1 1 0 1 0 0 0 0 1 0 0 1 1 0 0 0 0
1 0 1 0 1 1 1 1 1 1 1 0 1 0 0 0 0 1
0 0 0 0 0 1 0 0 0 0 0 0 0 0 1 0 0 0
0 0 1 1 0 1 1 1 0 0 0 1 1 0 1 1 1 0
0 1 1 1 1 1 0 1 1 0 1 1 1 1 1 0 1 1
1 1 0 1 1 1 0 1 1 1 0 1 0 0 0 1 0 1
0 0 1 0 0 1 1 1 1 0 0 1 0 0 1 1 1 1
0 1 1 0 1 0 1 0 1 0 1 1 0 1 0 1 0 1
1 1 1 1 0 1 1 1 0 1 0 0 0 1 0 0 1 0
1 1 0 1 0 1 1 1 1 1 0 1 0 1 0 0 0 1
0 0 1 1 0 1 1 0 1 0 0 1 1 0 1 1 0 1
1 1 0 1 0 0 0 0 0 1 0 1 1 0 0 0 0 0
1 0 1 1 1 1 1 0 1 1 1 0 0 0 0 0 1 1
0 0 1 1 0 0 0 1 0 0 0 1 1 0 0 0 1 0
0 1 0 0 1 0 1 0 0 0 1 0 0 1 0 1 0 0
1 1 1 1 0 1 0 0 1 1 0 0 0 1 0 1 1 1
1 0 0 1 0 1 1 0 1 1 1 1 0 1 0 0 1 1
1 0 0 0 0 0 1 1 1 1 1 1 1 1 1 0 0 1
0 1 0 1 1 0 0 0 0 0 1 0 1 1 0 0 0 0
0 1 0 0 0 1 0 1 0 0 1 0 0 0 1 0 1 0
0 1 0 0 1 0 1 0 1 0 1 0 0 1 0 1 0 1
1 1 1 0 1 1 1 0 0 1 0 0 1 0 0 1 0 0
0 0 0 1 1 1 0 0 0 0 0 0 1 1 1 0 0 0
1 0 1 1 1 0 0 1 0 1 1 0 0 0 1 1 1 0
1 1 1 1 0 0 0 1 0 1 0 0 0 1 1 1 1 0
1 0 0 0 1 0 1 0 0 1 1 1 1 0 1 1 0 0
1 1 1 1 0 1 0 0 1 1 0 0 0 1 0 1 1 1
0 1 1 1 0 0 1 0 1 0 1 1 1 0 0 1 0 1
0 1 1 0 0 1 0 0 1 0 1 1 0 0 1 0 0 1
1 1 0 1 0 1 1 0 0 1 0 1 0 1 0 1 0 0
0 0 1 0 1 1 0 0 1 0 0 1 0 1 1 0 0 1
0 0 1 0 0 1 1 1 0 0 0 1 0 0 1 1 1 0
1 0 1 1 0 0 1 0 1 1 1 0 0 1 1 0 1 1
0 0 1 1 1 1 1 1 0 0 0 1 1 1 1 1 1 0
1 0 1 1 0 1 0 0 1 1 1 0 0 1 0 1 1 1
1 1 0 1 0 0 1 0 1 1 0 1 0 1 1 0 1 1
0 1 0 1 1 1 1 0 0 0 1 0 1 1 1 1 0 0
0 1 1 0 1 0 0 0 1 0 1 1 0 1 0 0 0 1
0 0 0 1 1 1 1 0 0 0 0 0 1 1 1 1 0 0
0 0 1 1 1 0 0 0 0 0 0 1 1 1 0 0 0 0
0 0 1 1 0 0 1 0 0 0 0 1 1 0 0 1 0 0
1 0 1 0 1 0 0 0 1 1 1 0 1 0 1 1 1 1
0 1 1 1 0 1 1 0 0 0 1 1 1 0 1 1 0 0
0 0 1 0 0 0 1 1 0 0 0 1 0 0 0 1 1 0
0 0 1 0 0 0 0 0 1 0 0 1 0 0 0 0 0 1
1 0 1 0 0 0 1 0 0 1 1 0 1 1 1 1 0 0
1 1 0 1 0 0 0 0 0 1 0 1 1 0 0 0 0 0
0 1 1 1 1 1 0 0 1 0 1 1 1 1 1 0 0 1
0 0 0 0 0 0 1 0 1 0 0 0 0 0 0 1 0 1
1 0 1 0 1 0 0 1 0 1 1 0 1 0 1 1 1 0
0 1 0 0 1 0 1 0 1 0 1 0 0 1 0 1 0 1
0 1 0 1 1 1 0 0 1 0 1 0 1 1 1 0 0 1
0 0 1 1 0 0 0 0 0 0 0 1 1 0 0 0 0 0
1 0 0 1 0 1 0 0 0 1 1 1 0 1 1 0 0 0
0 0 0 1 0 1 0 0 0 0 0 0 1 0 1 0 0 0
1 1 1 1 1 0 0 1 0 1 0 0 0 0 1 1 1 0
0 0 0 1 1 1 0 0 0 0 0 0 1 1 1 0 0 0
1 0 1 0 0 1 1 1 0 1 1 0 1 1 0 0 1 0
0 0 0 1 1 0 1 0 1 0 0 0 1 1 0 1 0 1
0 0 0 1 0 1 0 0 0 0 0 0 1 0 1 0 0 0
1 0 1 0 0 0 0 0 1 1 1 0 1 1 1 1 1 1
1 0 1 0 0 1 0 1 1 1 1 0 1 1 0 1 0 1
0 0 0 1 0 1 0 0 1 0 0 0 1 0 1 0 0 1
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*/
